// Logisim project Space Invader.circ as structural Verilog: 6 circuits, main circuit main
module main (
);

  wire button_1_out, button_2_out;
  wire [2:0] bala_1_out_1;
  wire [3:0] \cpn_chip_posición_nave_1_output ;
  wire [7:0] cmnal_chip_mapeo_nave_a_led_1__0, cmnal_chip_mapeo_nave_a_led_1__0_2,
       cmnal_chip_mapeo_nave_a_led_1__0_3, cmnal_chip_mapeo_nave_a_led_1__0_4,
       cmnal_chip_mapeo_nave_a_led_1__0_5, cmnal_chip_mapeo_nave_a_led_1__0_6,
       cmnal_chip_mapeo_nave_a_led_1__0_7, cmnal_chip_mapeo_nave_a_led_1__0_8,
       cmnal_chip_mapeo_nave_a_led_1__0_9, cmnal_chip_mapeo_nave_a_led_1__0_10,
       cmnal_chip_mapeo_nave_a_led_1__0_11, cmnal_chip_mapeo_nave_a_led_1__0_12,
       cmnal_chip_mapeo_nave_a_led_1__0_13, cmnal_chip_mapeo_nave_a_led_1__0_14,
       cmnal_chip_mapeo_nave_a_led_1__0_15, cmnal_chip_mapeo_nave_a_led_1__0_16;

  Button button_1 (.out(button_1_out));
  Button button_2 (.out(button_2_out));
  \CPN___Chip_posición_nave  \cpn_chip_posición_nave_1  (
    .IZQ(button_1_out), .DER(button_2_out), .OUTPUT(\cpn_chip_posición_nave_1_output ));
  CMNAL___Chip_mapeo_nave_a_led cmnal_chip_mapeo_nave_a_led_1 (
    ._0(cmnal_chip_mapeo_nave_a_led_1__0[0]), ._1(cmnal_chip_mapeo_nave_a_led_1__0_2[1]),
    ._0_2(cmnal_chip_mapeo_nave_a_led_1__0_2[0]), ._1_2(cmnal_chip_mapeo_nave_a_led_1__0_3[1]),
    ._0_3(cmnal_chip_mapeo_nave_a_led_1__0_3[0]), ._1_3(cmnal_chip_mapeo_nave_a_led_1__0_4[1]),
    ._0_4(cmnal_chip_mapeo_nave_a_led_1__0_4[0]), ._1_4(cmnal_chip_mapeo_nave_a_led_1__0_5[1]),
    ._0_5(cmnal_chip_mapeo_nave_a_led_1__0_5[0]), ._1_5(cmnal_chip_mapeo_nave_a_led_1__0_6[1]),
    ._0_6(cmnal_chip_mapeo_nave_a_led_1__0_6[0]), ._1_6(cmnal_chip_mapeo_nave_a_led_1__0_7[1]),
    ._0_7(cmnal_chip_mapeo_nave_a_led_1__0_7[0]), ._1_7(cmnal_chip_mapeo_nave_a_led_1__0_8[1]),
    ._0_8(cmnal_chip_mapeo_nave_a_led_1__0_8[0]), ._1_8(cmnal_chip_mapeo_nave_a_led_1__0_9[1]),
    ._0_9(cmnal_chip_mapeo_nave_a_led_1__0_9[0]), ._1_9(cmnal_chip_mapeo_nave_a_led_1__0_10[1]),
    ._0_10(cmnal_chip_mapeo_nave_a_led_1__0_10[0]), ._1_10(cmnal_chip_mapeo_nave_a_led_1__0_11[1]),
    ._0_11(cmnal_chip_mapeo_nave_a_led_1__0_11[0]), ._1_11(cmnal_chip_mapeo_nave_a_led_1__0_12[1]),
    ._0_12(cmnal_chip_mapeo_nave_a_led_1__0_12[0]), ._1_12(cmnal_chip_mapeo_nave_a_led_1__0_13[1]),
    ._0_13(cmnal_chip_mapeo_nave_a_led_1__0_13[0]), ._1_13(cmnal_chip_mapeo_nave_a_led_1__0_14[1]),
    ._0_14(cmnal_chip_mapeo_nave_a_led_1__0_14[0]), ._1_14(cmnal_chip_mapeo_nave_a_led_1__0_15[1]),
    ._0_15(cmnal_chip_mapeo_nave_a_led_1__0_15[0]), ._0_16(cmnal_chip_mapeo_nave_a_led_1__0_16[0]),
    .INPUT(\cpn_chip_posición_nave_1_output ));
  Bala bala_1 (.out_1(bala_1_out_1));
  Decoder #(.select(3)) decoder_1 (
    .out2(cmnal_chip_mapeo_nave_a_led_1__0_2[2]), .out3(cmnal_chip_mapeo_nave_a_led_1__0_2[3]),
    .out4(cmnal_chip_mapeo_nave_a_led_1__0_2[4]), .out5(cmnal_chip_mapeo_nave_a_led_1__0_2[5]),
    .out6(cmnal_chip_mapeo_nave_a_led_1__0_2[6]), .out7(cmnal_chip_mapeo_nave_a_led_1__0_2[7]),
    .sel(bala_1_out_1));  // open: out0, out1, en
  DotMatrix #(.matrixcols(16), .matrixrows(8)) dotmatrix_1 (
    .col0({cmnal_chip_mapeo_nave_a_led_1__0[7:3], {2{cmnal_chip_mapeo_nave_a_led_1__0[3]}}, cmnal_chip_mapeo_nave_a_led_1__0[0]}),
    .col1(cmnal_chip_mapeo_nave_a_led_1__0_2), .col2(cmnal_chip_mapeo_nave_a_led_1__0_3),
    .col3(cmnal_chip_mapeo_nave_a_led_1__0_4), .col4(cmnal_chip_mapeo_nave_a_led_1__0_5),
    .col5(cmnal_chip_mapeo_nave_a_led_1__0_6), .col6(cmnal_chip_mapeo_nave_a_led_1__0_7),
    .col7(cmnal_chip_mapeo_nave_a_led_1__0_8), .col8(cmnal_chip_mapeo_nave_a_led_1__0_9),
    .col9(cmnal_chip_mapeo_nave_a_led_1__0_10), .col10(cmnal_chip_mapeo_nave_a_led_1__0_11),
    .col11(cmnal_chip_mapeo_nave_a_led_1__0_12), .col12(cmnal_chip_mapeo_nave_a_led_1__0_13),
    .col13(cmnal_chip_mapeo_nave_a_led_1__0_14), .col14(cmnal_chip_mapeo_nave_a_led_1__0_15),
    .col15(cmnal_chip_mapeo_nave_a_led_1__0_16));

  // Notes on the sheet:
  //   SP0
  //   SP15
endmodule

module \CPN___Chip_posición_nave  (
  input  IZQ,
  input  DER,
  output [3:0] OUTPUT
);

  wire and_1_out, and_2_out, and_3_out, and_4_out, and_5_out, and_6_out, and_7_out, and_8_out, and_9_out,
       and_10_out, and_11_out, and_12_out, and_13_out, and_14_out, and_15_out, and_16_out, and_17_out,
       and_18_out, and_19_out, and_20_out, and_21_out, and_22_out, and_23_out, and_24_out, and_25_out,
       and_26_out, and_27_out, and_28_out, and_29_out, and_30_out, and_31_out, and_32_out, and_33_out,
       and_34_out, and_35_out, and_36_out, not_1_out, not_2_out, not_3_out, not_4_out, not_5_out, not_6_out,
       not_7_out, not_8_out, not_9_out, not_10_out, not_11_out, not_12_out, not_13_out, not_14_out,
       not_15_out, not_16_out, not_17_out, not_18_out, not_19_out, not_20_out, not_21_out, not_22_out,
       not_23_out, not_24_out, not_25_out, not_26_out, not_27_out, not_28_out, not_29_out, not_30_out,
       not_31_out, not_32_out, not_33_out, not_34_out, not_35_out, not_36_out, not_37_out, not_38_out,
       not_39_out, not_40_out, not_41_out, not_42_out, not_43_out, not_44_out, not_45_out, not_46_out,
       not_47_out, not_48_out, not_49_out, not_50_out, not_51_out, not_52_out, not_53_out, not_54_out,
       not_55_out, not_56_out, not_57_out, not_58_out, or_1_out, or_2_out, or_3_out, or_4_out, or_5_out;

  and and_1 (and_1_out, DER, DER);
  and and_2 (and_2_out, IZQ, IZQ);
  not not_1 (not_1_out, IZQ);
  not not_2 (not_2_out, IZQ);
  not not_3 (not_3_out, OUTPUT[2]);
  not not_4 (not_4_out, IZQ);
  not not_5 (not_5_out, OUTPUT[1]);
  not not_6 (not_6_out, IZQ);
  not not_7 (not_7_out, IZQ);
  not not_8 (not_8_out, DER);
  not not_9 (not_9_out, OUTPUT[1]);
  not not_10 (not_10_out, OUTPUT[0]);
  not not_11 (not_11_out, OUTPUT[2]);
  not not_12 (not_12_out, OUTPUT[1]);
  not not_13 (not_13_out, OUTPUT[0]);
  not not_14 (not_14_out, DER);
  not not_15 (not_15_out, IZQ);
  not not_16 (not_16_out, OUTPUT[1]);
  not not_17 (not_17_out, IZQ);
  not not_18 (not_18_out, OUTPUT[0]);
  not not_19 (not_19_out, IZQ);
  not not_20 (not_20_out, DER);
  not not_21 (not_21_out, OUTPUT[1]);
  not not_22 (not_22_out, OUTPUT[0]);
  not not_23 (not_23_out, DER);
  not not_24 (not_24_out, OUTPUT[1]);
  not not_25 (not_25_out, OUTPUT[0]);
  not not_26 (not_26_out, DER);
  not not_27 (not_27_out, IZQ);
  not not_28 (not_28_out, OUTPUT[3]);
  not not_29 (not_29_out, OUTPUT[2]);
  not not_30 (not_30_out, OUTPUT[1]);
  not not_31 (not_31_out, OUTPUT[0]);
  not not_32 (not_32_out, OUTPUT[3]);
  not not_33 (not_33_out, OUTPUT[2]);
  not not_34 (not_34_out, OUTPUT[1]);
  not not_35 (not_35_out, DER);
  not not_36 (not_36_out, OUTPUT[3]);
  not not_37 (not_37_out, OUTPUT[0]);
  not not_38 (not_38_out, IZQ);
  not not_39 (not_39_out, OUTPUT[2]);
  not not_40 (not_40_out, OUTPUT[0]);
  not not_41 (not_41_out, IZQ);
  not not_42 (not_42_out, OUTPUT[1]);
  not not_43 (not_43_out, OUTPUT[0]);
  not not_44 (not_44_out, IZQ);
  not not_45 (not_45_out, OUTPUT[0]);
  not not_46 (not_46_out, DER);
  not not_47 (not_47_out, OUTPUT[3]);
  not not_48 (not_48_out, IZQ);
  not not_49 (not_49_out, DER);
  not not_50 (not_50_out, OUTPUT[2]);
  not not_51 (not_51_out, IZQ);
  not not_52 (not_52_out, DER);
  not not_53 (not_53_out, OUTPUT[1]);
  not not_54 (not_54_out, IZQ);
  not not_55 (not_55_out, DER);
  not not_56 (not_56_out, OUTPUT[3]);
  not not_57 (not_57_out, OUTPUT[2]);
  not not_58 (not_58_out, OUTPUT[1]);
  or or_1 (or_1_out, and_1_out, and_2_out);
  and and_3 (and_3_out, OUTPUT[2], OUTPUT[1], OUTPUT[0], not_1_out, DER);
  and and_4 (and_4_out, OUTPUT[3], not_2_out);
  and and_5 (and_5_out, OUTPUT[3], DER);
  and and_6 (and_6_out, OUTPUT[3], OUTPUT[0]);
  and and_7 (and_7_out, OUTPUT[3], OUTPUT[1]);
  and and_8 (and_8_out, OUTPUT[3], OUTPUT[2]);
  and and_9 (and_9_out, not_3_out, OUTPUT[1], OUTPUT[0], not_4_out, DER);
  and and_10 (and_10_out, OUTPUT[2], not_5_out, not_6_out);
  and and_11 (and_11_out, OUTPUT[2], not_7_out, not_8_out);
  and and_12 (and_12_out, OUTPUT[2], not_9_out, DER);
  and and_13 (and_13_out, OUTPUT[2], OUTPUT[0], IZQ);
  and and_14 (and_14_out, OUTPUT[2], OUTPUT[1], not_10_out);
  and and_15 (and_15_out, OUTPUT[3], not_11_out, not_12_out, not_13_out, IZQ, not_14_out);
  and and_16 (and_16_out, OUTPUT[3], OUTPUT[2], not_15_out);
  and and_17 (and_17_out, not_16_out, OUTPUT[0], not_17_out, DER);
  and and_18 (and_18_out, OUTPUT[1], not_18_out, not_19_out);
  and and_19 (and_19_out, OUTPUT[1], IZQ, DER);
  and and_20 (and_20_out, OUTPUT[1], OUTPUT[0], not_20_out);
  and and_21 (and_21_out, OUTPUT[2], not_21_out, not_22_out, IZQ, not_23_out);
  and and_22 (and_22_out, OUTPUT[3], not_24_out, not_25_out, IZQ, not_26_out);
  and and_23 (and_23_out, OUTPUT[3], OUTPUT[2], OUTPUT[1], not_27_out);
  and and_24 (and_24_out, not_28_out, not_29_out, not_30_out, not_31_out);
  and and_25 (and_25_out, not_32_out, not_33_out, not_34_out, not_35_out);
  and and_26 (and_26_out, not_36_out, not_37_out, not_38_out, DER);
  and and_27 (and_27_out, not_39_out, not_40_out, not_41_out, DER);
  and and_28 (and_28_out, not_42_out, not_43_out, not_44_out, DER);
  and and_29 (and_29_out, not_45_out, IZQ, not_46_out);
  and and_30 (and_30_out, not_47_out, OUTPUT[0], not_48_out, not_49_out);
  and and_31 (and_31_out, not_50_out, OUTPUT[0], not_51_out, not_52_out);
  and and_32 (and_32_out, not_53_out, OUTPUT[0], not_54_out, not_55_out);
  and and_33 (and_33_out, not_56_out, OUTPUT[0], IZQ, DER);
  and and_34 (and_34_out, not_57_out, OUTPUT[0], IZQ, DER);
  and and_35 (and_35_out, not_58_out, OUTPUT[0], IZQ, DER);
  or or_2 (or_2_out, and_3_out, and_4_out, and_5_out, and_6_out, and_7_out, and_8_out);
  or or_3 (or_3_out, and_17_out, and_18_out, and_19_out, and_20_out, and_21_out, and_22_out, and_23_out);
  and and_36 (and_36_out, or_1_out, or_1_out);
  or or_4 (or_4_out, and_9_out, and_10_out, and_11_out, and_12_out, and_13_out, and_14_out, and_15_out, and_16_out);
  or or_5 (or_5_out, and_24_out, and_25_out, and_26_out, and_27_out, and_28_out, and_29_out, and_30_out, and_31_out, and_32_out, and_33_out, and_34_out, and_35_out);
  D_Flip_Flop DA (.clk(and_36_out), .D(or_2_out), .Q(OUTPUT[3]));  // open: Qn, preset, en, reset
  D_Flip_Flop DB (.clk(and_36_out), .D(or_4_out), .Q(OUTPUT[2]));  // open: Qn, preset, en, reset
  D_Flip_Flop DC (.clk(and_36_out), .D(or_3_out), .Q(OUTPUT[1]));  // open: Qn, preset, en, reset
  D_Flip_Flop DD (.clk(and_36_out), .D(or_5_out), .Q(OUTPUT[0]));  // open: Qn, preset, en, reset

  // Notes on the sheet:
  //   INPUTS
  //   IMPLEMENTA EL MOVIMIENTO DEL PIXEL DE LA NAVE, TOMANDO COMO REFERENCIA EL PIXEL CENTRAL DE LA MISMA.
  //   EL OUTPUT SIMBOLIZA LA POSICIÓN EN LA FILA DEL PIXEL.
endmodule

module CMNAL___Chip_mapeo_nave_a_led (
  input  [3:0] INPUT,
  output _0,
  output _1,
  output _0_2,
  output _1_2,
  output _0_3,
  output _1_3,
  output _0_4,
  output _1_4,
  output _0_5,
  output _1_5,
  output _0_6,
  output _1_6,
  output _0_7,
  output _1_7,
  output _0_8,
  output _1_8,
  output _0_9,
  output _1_9,
  output _0_10,
  output _1_10,
  output _0_11,
  output _1_11,
  output _0_12,
  output _1_12,
  output _0_13,
  output _1_13,
  output _0_14,
  output _1_14,
  output _0_15,
  output _0_16
);

  Decoder #(.select(4)) decoder_1 (
    .out1(_0), .out2(_1_2), .out3(_1_3), .out4(_1_4), .out5(_1_5), .out6(_1_6), .out7(_1_7), .out8(_1_8),
    .out9(_1_9), .out10(_1_10), .out11(_1_11), .out12(_1_12), .out13(_1_13), .out14(_0_16), .sel(INPUT));  // open: out0, out15, en
  or u__1 (_0_2, _0, _1_2);
  or _2 (_0_3, _1_2, _0, _1_3);
  or _3 (_0_4, _1_2, _1_3, _1_4);
  or _4 (_0_5, _1_4, _1_3, _1_5);
  or _5 (_0_6, _1_4, _1_5, _1_6);
  or _6 (_0_7, _1_7, _1_5, _1_6);
  or _7 (_0_8, _1_7, _1_6, _1_8);
  or _8 (_0_9, _1_7, _1_8, _1_9);
  or _10 (_0_11, _1_9, _1_10, _1_11);
  or _9 (_0_10, _1_9, _1_10, _1_8);
  or _11 (_0_12, _1_10, _1_11, _1_12);
  or _12 (_0_13, _1_11, _1_12, _1_13);
  or _14 (_0_15, _1_13, _0_16);
  or _13 (_0_14, _1_12, _1_13, _0_16);

  assign _1 = _0;
  assign _1_14 = _0_16;

  // Notes on the sheet:
  //   OUTPUTS
  //   _sp1_
  //   sp0
  //   _sp2_
  //   _sp3_
  //   EL INPUT ESTÁ PENSADO PARA CONECTARLE LA SALIDA DEL CHIP DE POSICIÓN DE NAVE.
  //   _sp5_
  //   _sp4_
  //   _sp6_
  //   CADA OUTPUT TIENE ARRIBA LA ETIQUETA DE SU SPLITTER CORRESPONDIENTE. EL NÚMERO 0 O 1 INIDCA EL PIN DEL SPLITTER AL CUAL SE DEBE CONECTAR.
  //   _sp7_
  //   _sp8_
  //   _sp9_
  //   _sp10_
  //   _sp11_
  //   _sp12_
  //   _sp13_
  //   _sp14_
  //   sp15
endmodule

module navecitas (
);

  wire button_1_out, button_2_out, clock_1_out;
  wire [0:0] cmnal_chip_mapeo_nave_a_led_1__0, cmnal_chip_mapeo_nave_a_led_1__0_16;
  wire [1:0] cmnal_chip_mapeo_nave_a_led_1__0_2, cmnal_chip_mapeo_nave_a_led_1__0_3,
       cmnal_chip_mapeo_nave_a_led_1__0_4, cmnal_chip_mapeo_nave_a_led_1__0_5,
       cmnal_chip_mapeo_nave_a_led_1__0_6, cmnal_chip_mapeo_nave_a_led_1__0_7,
       cmnal_chip_mapeo_nave_a_led_1__0_8, cmnal_chip_mapeo_nave_a_led_1__0_9,
       cmnal_chip_mapeo_nave_a_led_1__0_10, cmnal_chip_mapeo_nave_a_led_1__0_11,
       cmnal_chip_mapeo_nave_a_led_1__0_12, cmnal_chip_mapeo_nave_a_led_1__0_13,
       cmnal_chip_mapeo_nave_a_led_1__0_14, cmnal_chip_mapeo_nave_a_led_1__0_15;
  wire [3:0] \cpn_chip_posición_nave_1_output ;

  Button button_1 (.out(button_1_out));
  Button button_2 (.out(button_2_out));
  \CPN___Chip_posición_nave  \cpn_chip_posición_nave_1  (
    .IZQ(button_1_out), .DER(button_2_out), .OUTPUT(\cpn_chip_posición_nave_1_output ));
  CMNAL___Chip_mapeo_nave_a_led cmnal_chip_mapeo_nave_a_led_1 (
    ._0(cmnal_chip_mapeo_nave_a_led_1__0[0]), ._1(cmnal_chip_mapeo_nave_a_led_1__0_2[1]),
    ._0_2(cmnal_chip_mapeo_nave_a_led_1__0_2[0]), ._1_2(cmnal_chip_mapeo_nave_a_led_1__0_3[1]),
    ._0_3(cmnal_chip_mapeo_nave_a_led_1__0_3[0]), ._1_3(cmnal_chip_mapeo_nave_a_led_1__0_4[1]),
    ._0_4(cmnal_chip_mapeo_nave_a_led_1__0_4[0]), ._1_4(cmnal_chip_mapeo_nave_a_led_1__0_5[1]),
    ._0_5(cmnal_chip_mapeo_nave_a_led_1__0_5[0]), ._1_5(cmnal_chip_mapeo_nave_a_led_1__0_6[1]),
    ._0_6(cmnal_chip_mapeo_nave_a_led_1__0_6[0]), ._1_6(cmnal_chip_mapeo_nave_a_led_1__0_7[1]),
    ._0_7(cmnal_chip_mapeo_nave_a_led_1__0_7[0]), ._1_7(cmnal_chip_mapeo_nave_a_led_1__0_8[1]),
    ._0_8(cmnal_chip_mapeo_nave_a_led_1__0_8[0]), ._1_8(cmnal_chip_mapeo_nave_a_led_1__0_9[1]),
    ._0_9(cmnal_chip_mapeo_nave_a_led_1__0_9[0]), ._1_9(cmnal_chip_mapeo_nave_a_led_1__0_10[1]),
    ._0_10(cmnal_chip_mapeo_nave_a_led_1__0_10[0]), ._1_10(cmnal_chip_mapeo_nave_a_led_1__0_11[1]),
    ._0_11(cmnal_chip_mapeo_nave_a_led_1__0_11[0]), ._1_11(cmnal_chip_mapeo_nave_a_led_1__0_12[1]),
    ._0_12(cmnal_chip_mapeo_nave_a_led_1__0_12[0]), ._1_12(cmnal_chip_mapeo_nave_a_led_1__0_13[1]),
    ._0_13(cmnal_chip_mapeo_nave_a_led_1__0_13[0]), ._1_13(cmnal_chip_mapeo_nave_a_led_1__0_14[1]),
    ._0_14(cmnal_chip_mapeo_nave_a_led_1__0_14[0]), ._1_14(cmnal_chip_mapeo_nave_a_led_1__0_15[1]),
    ._0_15(cmnal_chip_mapeo_nave_a_led_1__0_15[0]), ._0_16(cmnal_chip_mapeo_nave_a_led_1__0_16[0]),
    .INPUT(\cpn_chip_posición_nave_1_output ));
  Clock clock_1 (.out(clock_1_out));
  Counter #(.width(3), .max('h7), .ongoal("stay")) counter_1 (.clk(clock_1_out));  // open: load, D, count, Q, carry, clr
  DotMatrix #(.matrixcols(16), .matrixrows(8)) dotmatrix_1 (
    .col0({{7{1'b0}}, cmnal_chip_mapeo_nave_a_led_1__0[0]}),
    .col1({{6{1'b0}}, cmnal_chip_mapeo_nave_a_led_1__0_2}),
    .col2({6'b000010, cmnal_chip_mapeo_nave_a_led_1__0_3}),
    .col3({6'b000011, cmnal_chip_mapeo_nave_a_led_1__0_4}),
    .col4({6'b010010, cmnal_chip_mapeo_nave_a_led_1__0_5}),
    .col5({6'b011000, cmnal_chip_mapeo_nave_a_led_1__0_6}),
    .col6({6'b010000, cmnal_chip_mapeo_nave_a_led_1__0_7}),
    .col7({6'b000010, cmnal_chip_mapeo_nave_a_led_1__0_8}),
    .col8({6'b000011, cmnal_chip_mapeo_nave_a_led_1__0_9}),
    .col9({6'b000010, cmnal_chip_mapeo_nave_a_led_1__0_10}),
    .col10({6'b010000, cmnal_chip_mapeo_nave_a_led_1__0_11}),
    .col11({6'b011000, cmnal_chip_mapeo_nave_a_led_1__0_12}),
    .col12({6'b010010, cmnal_chip_mapeo_nave_a_led_1__0_13}),
    .col13({6'b000011, cmnal_chip_mapeo_nave_a_led_1__0_14}),
    .col14({6'b000010, cmnal_chip_mapeo_nave_a_led_1__0_15}),
    .col15({{7{1'b0}}, cmnal_chip_mapeo_nave_a_led_1__0_16[0]}));

  // Notes on the sheet:
  //   SP0
  //   SP15
endmodule

module Bala (
  output [2:0] out_1
);

  wire and_1_out, and_2_out, and_3_out, and_4_out, and_5_out, and_6_out, and_7_out, clock_1_out, d_ff_1_q,
       d_ff_2_q, d_ff_3_q, not_1_out, not_2_out, not_3_out, not_4_out, not_5_out, not_6_out, not_7_out;

  and and_1 (and_1_out, d_ff_1_q, d_ff_3_q);
  not not_1 (not_1_out, d_ff_2_q);
  not not_2 (not_2_out, d_ff_1_q);
  not not_3 (not_3_out, d_ff_3_q);
  not not_4 (not_4_out, d_ff_2_q);
  not not_5 (not_5_out, d_ff_3_q);
  not not_6 (not_6_out, d_ff_1_q);
  not not_7 (not_7_out, d_ff_3_q);
  or or_1 (out_1[2], and_1_out, d_ff_2_q);
  and and_2 (and_2_out, not_1_out, not_2_out, d_ff_3_q);
  and and_3 (and_3_out, d_ff_1_q, not_3_out);
  and and_4 (and_4_out, d_ff_2_q, d_ff_1_q);
  and and_5 (and_5_out, not_4_out, not_5_out);
  and and_6 (and_6_out, not_6_out, not_7_out);
  and and_7 (and_7_out, d_ff_2_q, d_ff_3_q);
  or or_2 (out_1[1], and_2_out, and_3_out, and_4_out);
  or or_3 (out_1[0], and_5_out, and_6_out, and_7_out);
  D_Flip_Flop d_ff_1 (.clk(clock_1_out), .D(out_1[1]), .Q(d_ff_1_q));  // open: Qn, preset, en, reset
  D_Flip_Flop d_ff_2 (.clk(clock_1_out), .D(out_1[2]), .Q(d_ff_2_q));  // open: Qn, preset, en, reset
  Clock clock_1 (.out(clock_1_out));
  D_Flip_Flop d_ff_3 (.clk(clock_1_out), .D(out_1[0]), .Q(d_ff_3_q));  // open: Qn, preset, en, reset
endmodule

module Balla (
  input  QA,
  input  QB,
  input  QC,
  output DA,
  output DB,
  output DC
);

  wire and_1_out, and_2_out, and_3_out, and_4_out, and_5_out, not_1_out, not_2_out, not_3_out, not_4_out,
       not_5_out;

  not not_1 (not_1_out, QA);
  not not_2 (not_2_out, QB);
  not not_3 (not_3_out, QC);
  not not_4 (not_4_out, QB);
  not not_5 (not_5_out, QC);
  not not_6 (DC, QC);
  and and_1 (and_1_out, not_1_out, QB, QC);
  and and_2 (and_2_out, QA, not_2_out);
  and and_3 (and_3_out, QA, not_3_out);
  and and_4 (and_4_out, not_4_out, QC);
  and and_5 (and_5_out, QB, not_5_out);
  or or_1 (DA, and_1_out, and_2_out, and_3_out);
  or or_2 (DB, and_4_out, and_5_out);
endmodule
