// Logisim project Space Invaders.circ as structural Verilog: 10 circuits, main circuit Placa madre - PM
module Pantalla_y_botones (
  input  POWER
);

  wire B_out, DER_out, IZQ_out;
  wire [7:0] placa_madre_pm_1_output_led_splitter, placa_madre_pm_1_output_led_splitter_2,
       placa_madre_pm_1_output_led_splitter_3, placa_madre_pm_1_output_led_splitter_4,
       placa_madre_pm_1_output_led_splitter_5, placa_madre_pm_1_output_led_splitter_6,
       placa_madre_pm_1_output_led_splitter_7, placa_madre_pm_1_output_led_splitter_8,
       placa_madre_pm_1_output_led_splitter_9, placa_madre_pm_1_output_led_splitter_10,
       placa_madre_pm_1_output_led_splitter_11, placa_madre_pm_1_output_led_splitter_12,
       placa_madre_pm_1_output_led_splitter_13, placa_madre_pm_1_output_led_splitter_14,
       placa_madre_pm_1_output_led_splitter_15, placa_madre_pm_1_output_led_splitter_16;

  DotMatrix #(.matrixcols(16), .matrixrows(8)) dotmatrix_1 (
    .col0(placa_madre_pm_1_output_led_splitter), .col1(placa_madre_pm_1_output_led_splitter_2),
    .col2(placa_madre_pm_1_output_led_splitter_3), .col3(placa_madre_pm_1_output_led_splitter_4),
    .col4(placa_madre_pm_1_output_led_splitter_5), .col5(placa_madre_pm_1_output_led_splitter_6),
    .col6(placa_madre_pm_1_output_led_splitter_7), .col7(placa_madre_pm_1_output_led_splitter_8),
    .col8(placa_madre_pm_1_output_led_splitter_9), .col9(placa_madre_pm_1_output_led_splitter_10),
    .col10(placa_madre_pm_1_output_led_splitter_11), .col11(placa_madre_pm_1_output_led_splitter_12),
    .col12(placa_madre_pm_1_output_led_splitter_13), .col13(placa_madre_pm_1_output_led_splitter_14),
    .col14(placa_madre_pm_1_output_led_splitter_15), .col15(placa_madre_pm_1_output_led_splitter_16));
  Placa_madre___PM placa_madre_pm_1 (
    .in_2(B_out), .\Input_botón_izquierda (IZQ_out), .\Input_botón_derecha (DER_out),
    .Output_Led_Splitter(placa_madre_pm_1_output_led_splitter),
    .Output_Led_Splitter_2(placa_madre_pm_1_output_led_splitter_2),
    .Output_Led_Splitter_3(placa_madre_pm_1_output_led_splitter_3),
    .Output_Led_Splitter_4(placa_madre_pm_1_output_led_splitter_4),
    .Output_Led_Splitter_5(placa_madre_pm_1_output_led_splitter_5),
    .Output_Led_Splitter_6(placa_madre_pm_1_output_led_splitter_6),
    .Output_Led_Splitter_7(placa_madre_pm_1_output_led_splitter_7),
    .Output_Led_Splitter_8(placa_madre_pm_1_output_led_splitter_8),
    .Output_Led_Splitter_9(placa_madre_pm_1_output_led_splitter_9),
    .Output_Led_Splitter_10(placa_madre_pm_1_output_led_splitter_10),
    .Output_Led_Splitter_11(placa_madre_pm_1_output_led_splitter_11),
    .Output_Led_Splitter_12(placa_madre_pm_1_output_led_splitter_12),
    .Output_Led_Splitter_13(placa_madre_pm_1_output_led_splitter_13),
    .Output_Led_Splitter_14(placa_madre_pm_1_output_led_splitter_14),
    .Output_Led_Splitter_15(placa_madre_pm_1_output_led_splitter_15),
    .Output_Led_Splitter_16(placa_madre_pm_1_output_led_splitter_16), .Input_power(POWER));
  Button IZQ (.out(IZQ_out));
  Button DER (.out(DER_out));
  Button B (.out(B_out));
endmodule

module Placa_madre___PM (
  input  Input_power,
  input  in_2,
  input  \Input_botón_izquierda ,
  input  \Input_botón_derecha ,
  output [7:0] Output_Led_Splitter,
  output [7:0] Output_Led_Splitter_2,
  output [7:0] Output_Led_Splitter_3,
  output [7:0] Output_Led_Splitter_4,
  output [7:0] Output_Led_Splitter_5,
  output [7:0] Output_Led_Splitter_6,
  output [7:0] Output_Led_Splitter_7,
  output [7:0] Output_Led_Splitter_8,
  output [7:0] Output_Led_Splitter_9,
  output [7:0] Output_Led_Splitter_10,
  output [7:0] Output_Led_Splitter_11,
  output [7:0] Output_Led_Splitter_12,
  output [7:0] Output_Led_Splitter_13,
  output [7:0] Output_Led_Splitter_14,
  output [7:0] Output_Led_Splitter_15,
  output [7:0] Output_Led_Splitter_16
);

  wire controlled_buffer_1_out, controlled_buffer_2_out, controlled_buffer_3_out;
  wire [0:0] chip_movimiento_nave_cmn_1_output_a_splitter_0__fila_0,
       chip_movimiento_nave_cmn_1_output_a_splitter_15___fila_0;
  wire [3:0] \chip_movimiento_nave_cmn_1_output_posición_nave ;
  wire [7:0] chip_movimiento_nave_cmn_1_output_a_splitter_1___fila_0,
       chip_movimiento_nave_cmn_1_output_a_splitter_2___fila_0,
       chip_movimiento_nave_cmn_1_output_a_splitter_3___fila_0,
       chip_movimiento_nave_cmn_1_output_a_splitter_4___fila_0,
       chip_movimiento_nave_cmn_1_output_a_splitter_5___fila_0,
       chip_movimiento_nave_cmn_1_output_a_splitter_6___fila_0,
       chip_movimiento_nave_cmn_1_output_a_splitter_7___fila_0,
       chip_movimiento_nave_cmn_1_output_a_splitter_8___fila_0,
       chip_movimiento_nave_cmn_1_output_a_splitter_9___fila_0,
       chip_movimiento_nave_cmn_1_output_a_splitter_10___fila_0,
       chip_movimiento_nave_cmn_1_output_a_splitter_11___fila_0,
       chip_movimiento_nave_cmn_1_output_a_splitter_12___fila_0,
       chip_movimiento_nave_cmn_1_output_a_splitter_13___fila_0,
       chip_movimiento_nave_cmn_1_output_a_splitter_14___fila_0;

  assign controlled_buffer_1_out = Input_power ? in_2 : 1'bz;  // Controlled_Buffer controlled_buffer_1
  assign controlled_buffer_2_out = Input_power ? \Input_botón_izquierda  : 1'bz;  // Controlled_Buffer controlled_buffer_2
  assign controlled_buffer_3_out = Input_power ? \Input_botón_derecha  : 1'bz;  // Controlled_Buffer controlled_buffer_3
  Chip_movimiento_nave___CMN chip_movimiento_nave_cmn_1 (
    .Output_a_splitter_0__fila_0(chip_movimiento_nave_cmn_1_output_a_splitter_0__fila_0[0]),
    .Output_a_splitter_1___Fila_1(chip_movimiento_nave_cmn_1_output_a_splitter_1___fila_0[1]),
    .Output_a_splitter_1___Fila_0(chip_movimiento_nave_cmn_1_output_a_splitter_1___fila_0[0]),
    .Output_a_splitter_2___Fila_1(chip_movimiento_nave_cmn_1_output_a_splitter_2___fila_0[1]),
    .Output_a_splitter_2___Fila_0(chip_movimiento_nave_cmn_1_output_a_splitter_2___fila_0[0]),
    .Output_a_splitter_3___Fila_1(chip_movimiento_nave_cmn_1_output_a_splitter_3___fila_0[1]),
    .Output_a_splitter_3___Fila_0(chip_movimiento_nave_cmn_1_output_a_splitter_3___fila_0[0]),
    .Output_a_splitter_4___Fila_1(chip_movimiento_nave_cmn_1_output_a_splitter_4___fila_0[1]),
    .Output_a_splitter_4___Fila_0(chip_movimiento_nave_cmn_1_output_a_splitter_4___fila_0[0]),
    .Output_a_splitter_5___Fila_1(chip_movimiento_nave_cmn_1_output_a_splitter_5___fila_0[1]),
    .Output_a_splitter_5___Fila_0(chip_movimiento_nave_cmn_1_output_a_splitter_5___fila_0[0]),
    .Output_a_splitter_6___Fila_1(chip_movimiento_nave_cmn_1_output_a_splitter_6___fila_0[1]),
    .Output_a_splitter_6___Fila_0(chip_movimiento_nave_cmn_1_output_a_splitter_6___fila_0[0]),
    .Output_a_splitter_7___Fila_1(chip_movimiento_nave_cmn_1_output_a_splitter_7___fila_0[1]),
    .Output_a_splitter_7___Fila_0(chip_movimiento_nave_cmn_1_output_a_splitter_7___fila_0[0]),
    .Output_a_splitter_8___Fila_1(chip_movimiento_nave_cmn_1_output_a_splitter_8___fila_0[1]),
    .Output_a_splitter_8___Fila_0(chip_movimiento_nave_cmn_1_output_a_splitter_8___fila_0[0]),
    .Output_a_splitter_9___Fila_1(chip_movimiento_nave_cmn_1_output_a_splitter_9___fila_0[1]),
    .Output_a_splitter_9___Fila_0(chip_movimiento_nave_cmn_1_output_a_splitter_9___fila_0[0]),
    .Output_a_splitter_10___Fila_1(chip_movimiento_nave_cmn_1_output_a_splitter_10___fila_0[1]),
    .Output_a_splitter_10___Fila_0(chip_movimiento_nave_cmn_1_output_a_splitter_10___fila_0[0]),
    .Output_a_splitter_11___Fila_1(chip_movimiento_nave_cmn_1_output_a_splitter_11___fila_0[1]),
    .Output_a_splitter_11___Fila_0(chip_movimiento_nave_cmn_1_output_a_splitter_11___fila_0[0]),
    .Output_a_splitter_12___Fila_1(chip_movimiento_nave_cmn_1_output_a_splitter_12___fila_0[1]),
    .Output_a_splitter_12___Fila_0(chip_movimiento_nave_cmn_1_output_a_splitter_12___fila_0[0]),
    .Output_a_splitter_13___Fila_1(chip_movimiento_nave_cmn_1_output_a_splitter_13___fila_0[1]),
    .Output_a_splitter_13___Fila_0(chip_movimiento_nave_cmn_1_output_a_splitter_13___fila_0[0]),
    .Output_a_splitter_14___Fila_1(chip_movimiento_nave_cmn_1_output_a_splitter_14___fila_0[1]),
    .Output_a_splitter_14___Fila_0(chip_movimiento_nave_cmn_1_output_a_splitter_14___fila_0[0]),
    .Output_a_splitter_15___Fila_0(chip_movimiento_nave_cmn_1_output_a_splitter_15___fila_0[0]),
    .\Output_posición_nave (\chip_movimiento_nave_cmn_1_output_posición_nave ), .Input_power(Input_power),
    .\Input_botón_izquierda (controlled_buffer_2_out), .\Input_botón_derecha (controlled_buffer_3_out));
  Chip_controlador_de_objetos___CCO chip_controlador_de_objetos_cco_1 (
    .\Input_posición_nave (\chip_movimiento_nave_cmn_1_output_posición_nave ),
    .Input_gatillo(controlled_buffer_1_out),
    .out_4(chip_movimiento_nave_cmn_1_output_a_splitter_1___fila_0[2]),
    .out_5(chip_movimiento_nave_cmn_1_output_a_splitter_1___fila_0[3]),
    .out_6(chip_movimiento_nave_cmn_1_output_a_splitter_1___fila_0[4]),
    .out_7(chip_movimiento_nave_cmn_1_output_a_splitter_1___fila_0[5]),
    .out_8(chip_movimiento_nave_cmn_1_output_a_splitter_1___fila_0[6]),
    .out_9(chip_movimiento_nave_cmn_1_output_a_splitter_1___fila_0[7]),
    .out_10(chip_movimiento_nave_cmn_1_output_a_splitter_2___fila_0[2]),
    .out_11(chip_movimiento_nave_cmn_1_output_a_splitter_2___fila_0[3]),
    .out_12(chip_movimiento_nave_cmn_1_output_a_splitter_2___fila_0[4]),
    .out_13(chip_movimiento_nave_cmn_1_output_a_splitter_2___fila_0[5]),
    .out_14(chip_movimiento_nave_cmn_1_output_a_splitter_2___fila_0[6]),
    .out_15(chip_movimiento_nave_cmn_1_output_a_splitter_2___fila_0[7]),
    .out_16(chip_movimiento_nave_cmn_1_output_a_splitter_3___fila_0[2]),
    .out_17(chip_movimiento_nave_cmn_1_output_a_splitter_3___fila_0[3]),
    .out_18(chip_movimiento_nave_cmn_1_output_a_splitter_3___fila_0[4]),
    .out_19(chip_movimiento_nave_cmn_1_output_a_splitter_3___fila_0[5]),
    .out_20(chip_movimiento_nave_cmn_1_output_a_splitter_3___fila_0[6]),
    .out_21(chip_movimiento_nave_cmn_1_output_a_splitter_3___fila_0[7]),
    .out_22(chip_movimiento_nave_cmn_1_output_a_splitter_4___fila_0[2]),
    .out_23(chip_movimiento_nave_cmn_1_output_a_splitter_4___fila_0[3]),
    .out_24(chip_movimiento_nave_cmn_1_output_a_splitter_4___fila_0[4]),
    .out_25(chip_movimiento_nave_cmn_1_output_a_splitter_4___fila_0[5]),
    .out_26(chip_movimiento_nave_cmn_1_output_a_splitter_4___fila_0[6]),
    .out_27(chip_movimiento_nave_cmn_1_output_a_splitter_4___fila_0[7]),
    .out_28(chip_movimiento_nave_cmn_1_output_a_splitter_5___fila_0[2]),
    .out_29(chip_movimiento_nave_cmn_1_output_a_splitter_5___fila_0[3]),
    .out_30(chip_movimiento_nave_cmn_1_output_a_splitter_5___fila_0[4]),
    .out_31(chip_movimiento_nave_cmn_1_output_a_splitter_5___fila_0[5]),
    .out_32(chip_movimiento_nave_cmn_1_output_a_splitter_5___fila_0[6]),
    .out_33(chip_movimiento_nave_cmn_1_output_a_splitter_5___fila_0[7]),
    .out_34(chip_movimiento_nave_cmn_1_output_a_splitter_6___fila_0[2]),
    .out_35(chip_movimiento_nave_cmn_1_output_a_splitter_6___fila_0[3]),
    .out_36(chip_movimiento_nave_cmn_1_output_a_splitter_6___fila_0[4]),
    .out_37(chip_movimiento_nave_cmn_1_output_a_splitter_6___fila_0[5]),
    .out_38(chip_movimiento_nave_cmn_1_output_a_splitter_6___fila_0[6]),
    .out_39(chip_movimiento_nave_cmn_1_output_a_splitter_6___fila_0[7]),
    .out_40(chip_movimiento_nave_cmn_1_output_a_splitter_7___fila_0[2]),
    .out_41(chip_movimiento_nave_cmn_1_output_a_splitter_7___fila_0[3]),
    .out_42(chip_movimiento_nave_cmn_1_output_a_splitter_7___fila_0[4]),
    .out_43(chip_movimiento_nave_cmn_1_output_a_splitter_7___fila_0[5]),
    .out_44(chip_movimiento_nave_cmn_1_output_a_splitter_7___fila_0[6]),
    .out_45(chip_movimiento_nave_cmn_1_output_a_splitter_7___fila_0[7]),
    .out_46(chip_movimiento_nave_cmn_1_output_a_splitter_8___fila_0[2]),
    .out_47(chip_movimiento_nave_cmn_1_output_a_splitter_8___fila_0[3]),
    .out_48(chip_movimiento_nave_cmn_1_output_a_splitter_8___fila_0[4]),
    .out_49(chip_movimiento_nave_cmn_1_output_a_splitter_8___fila_0[5]),
    .out_50(chip_movimiento_nave_cmn_1_output_a_splitter_8___fila_0[6]),
    .out_51(chip_movimiento_nave_cmn_1_output_a_splitter_8___fila_0[7]),
    .out_52(chip_movimiento_nave_cmn_1_output_a_splitter_9___fila_0[2]),
    .out_53(chip_movimiento_nave_cmn_1_output_a_splitter_9___fila_0[3]),
    .out_54(chip_movimiento_nave_cmn_1_output_a_splitter_9___fila_0[4]),
    .out_55(chip_movimiento_nave_cmn_1_output_a_splitter_9___fila_0[5]),
    .out_56(chip_movimiento_nave_cmn_1_output_a_splitter_9___fila_0[6]),
    .out_57(chip_movimiento_nave_cmn_1_output_a_splitter_9___fila_0[7]),
    .out_58(chip_movimiento_nave_cmn_1_output_a_splitter_10___fila_0[2]),
    .out_59(chip_movimiento_nave_cmn_1_output_a_splitter_10___fila_0[3]),
    .out_60(chip_movimiento_nave_cmn_1_output_a_splitter_10___fila_0[4]),
    .out_61(chip_movimiento_nave_cmn_1_output_a_splitter_10___fila_0[5]),
    .out_62(chip_movimiento_nave_cmn_1_output_a_splitter_10___fila_0[6]),
    .out_63(chip_movimiento_nave_cmn_1_output_a_splitter_10___fila_0[7]),
    .out_64(chip_movimiento_nave_cmn_1_output_a_splitter_11___fila_0[2]),
    .out_67(chip_movimiento_nave_cmn_1_output_a_splitter_11___fila_0[5]),
    .out_68(chip_movimiento_nave_cmn_1_output_a_splitter_11___fila_0[6]),
    .out_69(chip_movimiento_nave_cmn_1_output_a_splitter_11___fila_0[7]),
    .out_70(chip_movimiento_nave_cmn_1_output_a_splitter_12___fila_0[2]),
    .out_71(chip_movimiento_nave_cmn_1_output_a_splitter_12___fila_0[3]),
    .out_72(chip_movimiento_nave_cmn_1_output_a_splitter_12___fila_0[4]),
    .out_73(chip_movimiento_nave_cmn_1_output_a_splitter_12___fila_0[5]),
    .out_74(chip_movimiento_nave_cmn_1_output_a_splitter_12___fila_0[6]),
    .out_75(chip_movimiento_nave_cmn_1_output_a_splitter_12___fila_0[7]),
    .out_76(chip_movimiento_nave_cmn_1_output_a_splitter_13___fila_0[2]),
    .out_77(chip_movimiento_nave_cmn_1_output_a_splitter_13___fila_0[3]),
    .out_78(chip_movimiento_nave_cmn_1_output_a_splitter_13___fila_0[4]),
    .out_79(chip_movimiento_nave_cmn_1_output_a_splitter_13___fila_0[5]),
    .out_80(chip_movimiento_nave_cmn_1_output_a_splitter_13___fila_0[6]),
    .out_81(chip_movimiento_nave_cmn_1_output_a_splitter_13___fila_0[7]),
    .out_82(chip_movimiento_nave_cmn_1_output_a_splitter_14___fila_0[2]),
    .out_83(chip_movimiento_nave_cmn_1_output_a_splitter_14___fila_0[3]),
    .out_84(chip_movimiento_nave_cmn_1_output_a_splitter_14___fila_0[4]),
    .out_85(chip_movimiento_nave_cmn_1_output_a_splitter_14___fila_0[5]),
    .out_86(chip_movimiento_nave_cmn_1_output_a_splitter_14___fila_0[6]),
    .out_87(chip_movimiento_nave_cmn_1_output_a_splitter_14___fila_0[7]), .Input_power(Input_power),
    .out_66(chip_movimiento_nave_cmn_1_output_a_splitter_11___fila_0[4]),
    .out_65(chip_movimiento_nave_cmn_1_output_a_splitter_11___fila_0[3]));
  Power_switch_display___PSD power_switch_display_psd_1 (
    .Input_Power(Input_power),
    .Input_Led_Splitter({{7{1'b0}}, chip_movimiento_nave_cmn_1_output_a_splitter_0__fila_0[0]}),
    .Input_Led_Splitter_2(chip_movimiento_nave_cmn_1_output_a_splitter_1___fila_0),
    .Input_Led_Splitter_3(chip_movimiento_nave_cmn_1_output_a_splitter_2___fila_0),
    .Input_Led_Splitter_4(chip_movimiento_nave_cmn_1_output_a_splitter_3___fila_0),
    .Input_Led_Splitter_5(chip_movimiento_nave_cmn_1_output_a_splitter_4___fila_0),
    .Input_Led_Splitter_6(chip_movimiento_nave_cmn_1_output_a_splitter_5___fila_0),
    .Input_Led_Splitter_7(chip_movimiento_nave_cmn_1_output_a_splitter_6___fila_0),
    .Input_Led_Splitter_8(chip_movimiento_nave_cmn_1_output_a_splitter_7___fila_0),
    .Input_Led_Splitter_9(chip_movimiento_nave_cmn_1_output_a_splitter_8___fila_0),
    .Input_Led_Splitter_10(chip_movimiento_nave_cmn_1_output_a_splitter_9___fila_0),
    .Input_Led_Splitter_11(chip_movimiento_nave_cmn_1_output_a_splitter_10___fila_0),
    .Input_Led_Splitter_12(chip_movimiento_nave_cmn_1_output_a_splitter_11___fila_0),
    .Input_Led_Splitter_13(chip_movimiento_nave_cmn_1_output_a_splitter_12___fila_0),
    .Input_Led_Splitter_14(chip_movimiento_nave_cmn_1_output_a_splitter_13___fila_0),
    .Output_Led_Splitter(Output_Led_Splitter), .Output_Led_Splitter_2(Output_Led_Splitter_2),
    .Output_Led_Splitter_3(Output_Led_Splitter_3), .Output_Led_Splitter_4(Output_Led_Splitter_4),
    .Output_Led_Splitter_5(Output_Led_Splitter_5), .Output_Led_Splitter_6(Output_Led_Splitter_6),
    .Output_Led_Splitter_7(Output_Led_Splitter_7), .Output_Led_Splitter_8(Output_Led_Splitter_8),
    .Output_Led_Splitter_9(Output_Led_Splitter_9), .Output_Led_Splitter_10(Output_Led_Splitter_10),
    .Output_Led_Splitter_11(Output_Led_Splitter_11), .Output_Led_Splitter_12(Output_Led_Splitter_12),
    .Output_Led_Splitter_13(Output_Led_Splitter_13), .Output_Led_Splitter_14(Output_Led_Splitter_14),
    .Input_Led_Splitter_15(chip_movimiento_nave_cmn_1_output_a_splitter_14___fila_0),
    .Input_Led_Splitter_16({{7{1'b0}}, chip_movimiento_nave_cmn_1_output_a_splitter_15___fila_0[0]}),
    .Output_Led_Splitter_15(Output_Led_Splitter_15), .Output_Led_Splitter_16(Output_Led_Splitter_16));

  // Notes on the sheet:
  //   SP0
  //   SP15
  //   PANTALLA LED 8x16
endmodule

module Chip_controlador_de_objetos___CCO (
  input  Input_power,
  input  [3:0] \Input_posición_nave ,
  input  Input_gatillo,
  output out_4,
  output out_5,
  output out_6,
  output out_7,
  output out_8,
  output out_9,
  output out_10,
  output out_11,
  output out_12,
  output out_13,
  output out_14,
  output out_15,
  output out_16,
  output out_17,
  output out_18,
  output out_19,
  output out_20,
  output out_21,
  output out_22,
  output out_23,
  output out_24,
  output out_25,
  output out_26,
  output out_27,
  output out_28,
  output out_29,
  output out_30,
  output out_31,
  output out_32,
  output out_33,
  output out_34,
  output out_35,
  output out_36,
  output out_37,
  output out_38,
  output out_39,
  output out_40,
  output out_41,
  output out_42,
  output out_43,
  output out_44,
  output out_45,
  output out_46,
  output out_47,
  output out_48,
  output out_49,
  output out_50,
  output out_51,
  output out_52,
  output out_53,
  output out_54,
  output out_55,
  output out_56,
  output out_57,
  output out_58,
  output out_59,
  output out_60,
  output out_61,
  output out_62,
  output out_63,
  output out_64,
  output out_65,
  output out_66,
  output out_67,
  output out_68,
  output out_69,
  output out_70,
  output out_71,
  output out_72,
  output out_73,
  output out_74,
  output out_75,
  output out_76,
  output out_77,
  output out_78,
  output out_79,
  output out_80,
  output out_81,
  output out_82,
  output out_83,
  output out_84,
  output out_85,
  output out_86,
  output out_87
);

  wire and_1_out, and_2_out, and_3_out, and_4_out, and_5_out, and_6_out, and_7_out, and_8_out, and_9_out,
       and_10_out, and_11_out, and_12_out, and_13_out, and_14_out, and_15_out,
       \chip_controlador_colisiónes_cc_1_output_colisión_invasor_1 ,
       \chip_controlador_colisiónes_cc_1_output_colisión_invasor_2 ,
       \chip_controlador_colisiónes_cc_1_output_colisión_invasor_3 ,
       \chip_controlador_colisiónes_cc_1_output_colisión_invasor_4 ,
       \chip_controlador_colisiónes_cc_1_output_colisión_invasor_5 ,
       chip_controlador_invasores_cci_1_output_invasor_1_encendido,
       chip_controlador_invasores_cci_1_output_invasor_2_encendido,
       chip_controlador_invasores_cci_1_output_invasor_3_encendido,
       chip_controlador_invasores_cci_1_output_invasor_4_encendido,
       chip_controlador_invasores_cci_1_output_invasor_5_encendido, decoder_1_out1, decoder_1_out2,
       decoder_1_out3, decoder_1_out4, decoder_1_out5, decoder_1_out6, decoder_1_out7, decoder_1_out8,
       decoder_1_out9, decoder_1_out10, decoder_1_out11, decoder_1_out12, decoder_1_out13, decoder_1_out14,
       not_1_out, or_1_out, \SP_1_output__registro_activo__sí__1 , SP_2_output_a_fila_3_splitter,
       SP_3_output_a_fila_2_splitter, SP_3_output_a_fila_3_splitter, SP_4_output_a_fila_3_splitter,
       SP_4_output_a_fila_6_splitter, SP_5_output_a_fila_5_splitter, SP_5_output_a_fila_6_splitter,
       SP_6_output_a_fila_6_splitter, SP_7_output_a_fila_3_splitter, SP_8_output_a_fila_2_splitter,
       SP_8_output_a_fila_3_splitter, SP_9_output_a_fila_3_splitter, SP_10_output_a_fila_6_splitter,
       SP_11_output_a_fila_5_splitter, SP_11_output_a_fila_6_splitter, SP_12_output_a_fila_3_splitter,
       SP_12_output_a_fila_6_splitter, SP_13_output_a_fila_2_splitter, SP_13_output_a_fila_3_splitter,
       SP_14_output_a_fila_3_splitter;

  Decoder #(.select(4)) decoder_1 (
    .out1(decoder_1_out1), .out2(decoder_1_out2), .out3(decoder_1_out3), .out4(decoder_1_out4),
    .out5(decoder_1_out5), .out6(decoder_1_out6), .out7(decoder_1_out7), .out8(decoder_1_out8),
    .out9(decoder_1_out9), .out10(decoder_1_out10), .out11(decoder_1_out11), .out12(decoder_1_out12),
    .out13(decoder_1_out13), .out14(decoder_1_out14), .sel(\Input_posición_nave ));  // open: out0, out15, en
  and and_1 (and_1_out, Input_gatillo, not_1_out);
  not not_1 (not_1_out, \SP_1_output__registro_activo__sí__1 );
  and and_2 (and_2_out, decoder_1_out1, and_1_out);
  and and_3 (and_3_out, decoder_1_out2, and_1_out);
  and and_4 (and_4_out, decoder_1_out3, and_1_out);
  and and_5 (and_5_out, decoder_1_out4, and_1_out);
  and and_6 (and_6_out, decoder_1_out5, and_1_out);
  and and_7 (and_7_out, decoder_1_out6, and_1_out);
  and and_8 (and_8_out, decoder_1_out7, and_1_out);
  and and_9 (and_9_out, decoder_1_out8, and_1_out);
  and and_10 (and_10_out, decoder_1_out9, and_1_out);
  and and_11 (and_11_out, decoder_1_out10, and_1_out);
  and and_12 (and_12_out, decoder_1_out11, and_1_out);
  and and_13 (and_13_out, decoder_1_out12, and_1_out);
  and and_14 (and_14_out, decoder_1_out13, and_1_out);
  and and_15 (and_15_out, decoder_1_out14, and_1_out);
  Chip_desplazamiento_bala___CDB SP_1 (
    .Input_gatillo(and_2_out), .Output_a_fila_2_splitter(out_4), .Output_a_fila_3_splitter(out_5),
    .Output_a_fila_4_splitter(out_6), .Output_a_fila_5_splitter(out_7), .Output_a_fila_6_splitter(out_8),
    .Output_a_fila_7_splitter(out_9),
    .\Output__Registro_activo__Sí__1 (\SP_1_output__registro_activo__sí__1 ), .Input_power(Input_power),
    .Input__Reset___1__Limpia_el_registro(or_1_out));
  Chip_desplazamiento_bala___CDB SP_2 (
    .Input_gatillo(and_3_out), .Output_a_fila_2_splitter(out_10),
    .Output_a_fila_3_splitter(SP_2_output_a_fila_3_splitter), .Output_a_fila_4_splitter(out_12),
    .Output_a_fila_5_splitter(out_13), .Output_a_fila_6_splitter(out_14), .Output_a_fila_7_splitter(out_15),
    .\Output__Registro_activo__Sí__1 (\SP_1_output__registro_activo__sí__1 ), .Input_power(Input_power),
    .Input__Reset___1__Limpia_el_registro(or_1_out));
  Chip_desplazamiento_bala___CDB SP_3 (
    .Input_gatillo(and_4_out), .Output_a_fila_2_splitter(SP_3_output_a_fila_2_splitter),
    .Output_a_fila_3_splitter(SP_3_output_a_fila_3_splitter), .Output_a_fila_4_splitter(out_18),
    .Output_a_fila_5_splitter(out_19), .Output_a_fila_6_splitter(out_20), .Output_a_fila_7_splitter(out_21),
    .\Output__Registro_activo__Sí__1 (\SP_1_output__registro_activo__sí__1 ), .Input_power(Input_power),
    .Input__Reset___1__Limpia_el_registro(or_1_out));
  Chip_desplazamiento_bala___CDB SP_4 (
    .Input_gatillo(and_5_out), .Output_a_fila_2_splitter(out_22),
    .Output_a_fila_3_splitter(SP_4_output_a_fila_3_splitter), .Output_a_fila_4_splitter(out_24),
    .Output_a_fila_5_splitter(out_25), .Output_a_fila_6_splitter(SP_4_output_a_fila_6_splitter),
    .Output_a_fila_7_splitter(out_27),
    .\Output__Registro_activo__Sí__1 (\SP_1_output__registro_activo__sí__1 ), .Input_power(Input_power),
    .Input__Reset___1__Limpia_el_registro(or_1_out));
  Chip_desplazamiento_bala___CDB SP_5 (
    .Input_gatillo(and_6_out), .Output_a_fila_2_splitter(out_28), .Output_a_fila_3_splitter(out_29),
    .Output_a_fila_4_splitter(out_30), .Output_a_fila_5_splitter(SP_5_output_a_fila_5_splitter),
    .Output_a_fila_6_splitter(SP_5_output_a_fila_6_splitter), .Output_a_fila_7_splitter(out_33),
    .\Output__Registro_activo__Sí__1 (\SP_1_output__registro_activo__sí__1 ), .Input_power(Input_power),
    .Input__Reset___1__Limpia_el_registro(or_1_out));
  Chip_desplazamiento_bala___CDB SP_6 (
    .Input_gatillo(and_7_out), .Output_a_fila_2_splitter(out_34), .Output_a_fila_3_splitter(out_35),
    .Output_a_fila_4_splitter(out_36), .Output_a_fila_5_splitter(out_37),
    .Output_a_fila_6_splitter(SP_6_output_a_fila_6_splitter), .Output_a_fila_7_splitter(out_39),
    .\Output__Registro_activo__Sí__1 (\SP_1_output__registro_activo__sí__1 ), .Input_power(Input_power),
    .Input__Reset___1__Limpia_el_registro(or_1_out));
  Chip_desplazamiento_bala___CDB SP_7 (
    .Input_gatillo(and_8_out), .Output_a_fila_2_splitter(out_40),
    .Output_a_fila_3_splitter(SP_7_output_a_fila_3_splitter), .Output_a_fila_4_splitter(out_42),
    .Output_a_fila_5_splitter(out_43), .Output_a_fila_6_splitter(out_44), .Output_a_fila_7_splitter(out_45),
    .\Output__Registro_activo__Sí__1 (\SP_1_output__registro_activo__sí__1 ), .Input_power(Input_power),
    .Input__Reset___1__Limpia_el_registro(or_1_out));
  Chip_desplazamiento_bala___CDB SP_8 (
    .Input_gatillo(and_9_out), .Output_a_fila_2_splitter(SP_8_output_a_fila_2_splitter),
    .Output_a_fila_3_splitter(SP_8_output_a_fila_3_splitter), .Output_a_fila_4_splitter(out_48),
    .Output_a_fila_5_splitter(out_49), .Output_a_fila_6_splitter(out_50), .Output_a_fila_7_splitter(out_51),
    .\Output__Registro_activo__Sí__1 (\SP_1_output__registro_activo__sí__1 ), .Input_power(Input_power),
    .Input__Reset___1__Limpia_el_registro(or_1_out));
  Chip_desplazamiento_bala___CDB SP_9 (
    .Input_gatillo(and_10_out), .Output_a_fila_2_splitter(out_52),
    .Output_a_fila_3_splitter(SP_9_output_a_fila_3_splitter), .Output_a_fila_4_splitter(out_54),
    .Output_a_fila_5_splitter(out_55), .Output_a_fila_6_splitter(out_56), .Output_a_fila_7_splitter(out_57),
    .\Output__Registro_activo__Sí__1 (\SP_1_output__registro_activo__sí__1 ), .Input_power(Input_power),
    .Input__Reset___1__Limpia_el_registro(or_1_out));
  Chip_desplazamiento_bala___CDB SP_10 (
    .Input_gatillo(and_11_out), .Output_a_fila_2_splitter(out_58), .Output_a_fila_3_splitter(out_59),
    .Output_a_fila_4_splitter(out_60), .Output_a_fila_5_splitter(out_61),
    .Output_a_fila_6_splitter(SP_10_output_a_fila_6_splitter), .Output_a_fila_7_splitter(out_63),
    .\Output__Registro_activo__Sí__1 (\SP_1_output__registro_activo__sí__1 ), .Input_power(Input_power),
    .Input__Reset___1__Limpia_el_registro(or_1_out));
  Chip_desplazamiento_bala___CDB SP_11 (
    .Input_gatillo(and_12_out), .Output_a_fila_2_splitter(out_64), .Output_a_fila_3_splitter(out_65),
    .Output_a_fila_4_splitter(out_66), .Output_a_fila_5_splitter(SP_11_output_a_fila_5_splitter),
    .Output_a_fila_6_splitter(SP_11_output_a_fila_6_splitter), .Output_a_fila_7_splitter(out_69),
    .\Output__Registro_activo__Sí__1 (\SP_1_output__registro_activo__sí__1 ), .Input_power(Input_power),
    .Input__Reset___1__Limpia_el_registro(or_1_out));
  Chip_desplazamiento_bala___CDB SP_12 (
    .Input_gatillo(and_13_out), .Output_a_fila_2_splitter(out_70),
    .Output_a_fila_3_splitter(SP_12_output_a_fila_3_splitter), .Output_a_fila_4_splitter(out_72),
    .Output_a_fila_5_splitter(out_73), .Output_a_fila_6_splitter(SP_12_output_a_fila_6_splitter),
    .Output_a_fila_7_splitter(out_75),
    .\Output__Registro_activo__Sí__1 (\SP_1_output__registro_activo__sí__1 ), .Input_power(Input_power),
    .Input__Reset___1__Limpia_el_registro(or_1_out));
  Chip_desplazamiento_bala___CDB SP_13 (
    .Input_gatillo(and_14_out), .Output_a_fila_2_splitter(SP_13_output_a_fila_2_splitter),
    .Output_a_fila_3_splitter(SP_13_output_a_fila_3_splitter), .Output_a_fila_4_splitter(out_78),
    .Output_a_fila_5_splitter(out_79), .Output_a_fila_6_splitter(out_80), .Output_a_fila_7_splitter(out_81),
    .\Output__Registro_activo__Sí__1 (\SP_1_output__registro_activo__sí__1 ), .Input_power(Input_power),
    .Input__Reset___1__Limpia_el_registro(or_1_out));
  Chip_desplazamiento_bala___CDB SP_14 (
    .Input_gatillo(and_15_out), .Output_a_fila_2_splitter(out_82),
    .Output_a_fila_3_splitter(SP_14_output_a_fila_3_splitter), .Output_a_fila_4_splitter(out_84),
    .Output_a_fila_5_splitter(out_85), .Output_a_fila_6_splitter(out_86), .Output_a_fila_7_splitter(out_87),
    .\Output__Registro_activo__Sí__1 (\SP_1_output__registro_activo__sí__1 ), .Input_power(Input_power),
    .Input__Reset___1__Limpia_el_registro(or_1_out));
  or or_1 (or_1_out, \chip_controlador_colisiónes_cc_1_output_colisión_invasor_1 , \chip_controlador_colisiónes_cc_1_output_colisión_invasor_2 , \chip_controlador_colisiónes_cc_1_output_colisión_invasor_3 , \chip_controlador_colisiónes_cc_1_output_colisión_invasor_4 , \chip_controlador_colisiónes_cc_1_output_colisión_invasor_5 );
  \Chip_controlador_colisiónes___CC  \chip_controlador_colisiónes_cc_1  (
    .Puerta_3_invasor_1(SP_2_output_a_fila_3_splitter), .Puerta_2_invasor_1(SP_3_output_a_fila_2_splitter),
    .Puerta_3_invasor_1_2(SP_4_output_a_fila_3_splitter),
    .\Output_colisión_invasor_1 (\chip_controlador_colisiónes_cc_1_output_colisión_invasor_1 ),
    .Puerta_6_invasor_2(SP_4_output_a_fila_6_splitter),
    .\Output_colisión_invasor_2 (\chip_controlador_colisiónes_cc_1_output_colisión_invasor_2 ),
    .Puerta_5_invasor_2(SP_5_output_a_fila_5_splitter), .Puerta_6_invasor_2_2(SP_6_output_a_fila_6_splitter),
    .Puerta_3_invasor_3(SP_7_output_a_fila_3_splitter),
    .\Output_colisión_invasor_3 (\chip_controlador_colisiónes_cc_1_output_colisión_invasor_3 ),
    .Puerta_2_invasor_3(SP_8_output_a_fila_2_splitter), .Puerta_3_invasor_3_2(SP_9_output_a_fila_3_splitter),
    .Puerta_6_invasor_4(SP_10_output_a_fila_6_splitter),
    .\Output_colisión_invasor_4 (\chip_controlador_colisiónes_cc_1_output_colisión_invasor_4 ),
    .Puerta_5_invasor_4(SP_11_output_a_fila_5_splitter),
    .Puerta_6_invasor_4_2(SP_12_output_a_fila_6_splitter),
    .Puerta_3_invasor_5(SP_12_output_a_fila_3_splitter),
    .\Output_colisión_invasor_5 (\chip_controlador_colisiónes_cc_1_output_colisión_invasor_5 ),
    .Puerta_2_invasor_5(SP_13_output_a_fila_2_splitter),
    .Puerta_3_invasor_5_2(SP_14_output_a_fila_3_splitter),
    .Input_invasor_1(chip_controlador_invasores_cci_1_output_invasor_1_encendido),
    .Input_invasor_2(chip_controlador_invasores_cci_1_output_invasor_2_encendido),
    .Input_invasor_3(chip_controlador_invasores_cci_1_output_invasor_3_encendido),
    .Input_invasor_4(chip_controlador_invasores_cci_1_output_invasor_4_encendido),
    .Input_invasor_5(chip_controlador_invasores_cci_1_output_invasor_5_encendido));
  or _2 (out_16, chip_controlador_invasores_cci_1_output_invasor_1_encendido, SP_3_output_a_fila_2_splitter);
  or _3 (out_11, chip_controlador_invasores_cci_1_output_invasor_1_encendido, SP_2_output_a_fila_3_splitter);
  or _3_2 (out_17, chip_controlador_invasores_cci_1_output_invasor_1_encendido, SP_3_output_a_fila_3_splitter);
  or _3_3 (out_23, chip_controlador_invasores_cci_1_output_invasor_1_encendido, SP_4_output_a_fila_3_splitter);
  or _5 (out_31, chip_controlador_invasores_cci_1_output_invasor_2_encendido, SP_5_output_a_fila_5_splitter);
  or _6 (out_26, chip_controlador_invasores_cci_1_output_invasor_2_encendido, SP_4_output_a_fila_6_splitter);
  or _6_2 (out_32, chip_controlador_invasores_cci_1_output_invasor_2_encendido, SP_5_output_a_fila_6_splitter);
  or _6_3 (out_38, chip_controlador_invasores_cci_1_output_invasor_2_encendido, SP_6_output_a_fila_6_splitter);
  or _2_2 (out_46, chip_controlador_invasores_cci_1_output_invasor_3_encendido, SP_8_output_a_fila_2_splitter);
  or _3_4 (out_41, chip_controlador_invasores_cci_1_output_invasor_3_encendido, SP_7_output_a_fila_3_splitter);
  or _3_5 (out_47, chip_controlador_invasores_cci_1_output_invasor_3_encendido, SP_8_output_a_fila_3_splitter);
  or _3_6 (out_53, chip_controlador_invasores_cci_1_output_invasor_3_encendido, SP_9_output_a_fila_3_splitter);
  or _6_4 (out_62, chip_controlador_invasores_cci_1_output_invasor_4_encendido, SP_10_output_a_fila_6_splitter);
  or _5_2 (out_67, chip_controlador_invasores_cci_1_output_invasor_4_encendido, SP_11_output_a_fila_5_splitter);
  or _6_5 (out_68, chip_controlador_invasores_cci_1_output_invasor_4_encendido, SP_11_output_a_fila_6_splitter);
  or _6_6 (out_74, chip_controlador_invasores_cci_1_output_invasor_4_encendido, SP_12_output_a_fila_6_splitter);
  or _2_3 (out_76, chip_controlador_invasores_cci_1_output_invasor_5_encendido, SP_13_output_a_fila_2_splitter);
  Chip_controlador_invasores___CCI chip_controlador_invasores_cci_1 (
    .Input_power(Input_power),
    .Input_apagar_invasor_1(\chip_controlador_colisiónes_cc_1_output_colisión_invasor_1 ),
    .Input_apagar_invasor_2(\chip_controlador_colisiónes_cc_1_output_colisión_invasor_2 ),
    .Input_apagar_invasor_3(\chip_controlador_colisiónes_cc_1_output_colisión_invasor_3 ),
    .Input_apagar_invasor_4(\chip_controlador_colisiónes_cc_1_output_colisión_invasor_4 ),
    .Input_apagar_invasor_5(\chip_controlador_colisiónes_cc_1_output_colisión_invasor_5 ),
    .Output_invasor_1_encendido(chip_controlador_invasores_cci_1_output_invasor_1_encendido),
    .Output_invasor_2_encendido(chip_controlador_invasores_cci_1_output_invasor_2_encendido),
    .Output_invasor_3_encendido(chip_controlador_invasores_cci_1_output_invasor_3_encendido),
    .Output_invasor_4_encendido(chip_controlador_invasores_cci_1_output_invasor_4_encendido),
    .Output_invasor_5_encendido(chip_controlador_invasores_cci_1_output_invasor_5_encendido));
  or _3_7 (out_71, chip_controlador_invasores_cci_1_output_invasor_5_encendido, SP_12_output_a_fila_3_splitter);
  or _3_8 (out_77, chip_controlador_invasores_cci_1_output_invasor_5_encendido, SP_13_output_a_fila_3_splitter);
  or _3_9 (out_83, chip_controlador_invasores_cci_1_output_invasor_5_encendido, SP_14_output_a_fila_3_splitter);

  // Notes on the sheet:
  //   ESTO ÚLTIMO QUIERE DECIR QUE HAY UNA BALA RECORRIENDO OTRO REGISTRO. ASÍ SE EVITA QUE SE PUEDA DISPARAR OTRA BALA MIENTRAS HAYA UNA ACTIVA
endmodule

module Chip_controlador_invasores___CCI (
  input  Input_power,
  input  Input_apagar_invasor_1,
  input  Input_apagar_invasor_2,
  input  Input_apagar_invasor_3,
  input  Input_apagar_invasor_4,
  input  Input_apagar_invasor_5,
  output Output_invasor_1_encendido,
  output Output_invasor_2_encendido,
  output Output_invasor_3_encendido,
  output Output_invasor_4_encendido,
  output Output_invasor_5_encendido
);

  Chip_Invasor___CI INV1 (
    .Input_power(Input_power), .Input__Apagar_nave__Apagar__1(Input_apagar_invasor_1),
    .\Output__Nave_encedida__Sí__1 (Output_invasor_1_encendido));
  Chip_Invasor___CI INV2 (
    .Input_power(Input_power), .Input__Apagar_nave__Apagar__1(Input_apagar_invasor_2),
    .\Output__Nave_encedida__Sí__1 (Output_invasor_2_encendido));
  Chip_Invasor___CI INV3 (
    .Input_power(Input_power), .Input__Apagar_nave__Apagar__1(Input_apagar_invasor_3),
    .\Output__Nave_encedida__Sí__1 (Output_invasor_3_encendido));
  Chip_Invasor___CI INV4 (
    .Input_power(Input_power), .Input__Apagar_nave__Apagar__1(Input_apagar_invasor_4),
    .\Output__Nave_encedida__Sí__1 (Output_invasor_4_encendido));
  Chip_Invasor___CI INV5 (
    .Input_power(Input_power), .Input__Apagar_nave__Apagar__1(Input_apagar_invasor_5),
    .\Output__Nave_encedida__Sí__1 (Output_invasor_5_encendido));
endmodule

module \Chip_controlador_colisiónes___CC  (
  input  Input_invasor_1,
  input  Puerta_3_invasor_1,
  input  Puerta_2_invasor_1,
  input  Puerta_3_invasor_1_2,
  input  Input_invasor_2,
  input  Puerta_6_invasor_2,
  input  Puerta_5_invasor_2,
  input  Puerta_6_invasor_2_2,
  input  Input_invasor_3,
  input  Puerta_3_invasor_3,
  input  Puerta_2_invasor_3,
  input  Puerta_3_invasor_3_2,
  input  Input_invasor_4,
  input  Puerta_6_invasor_4,
  input  Puerta_5_invasor_4,
  input  Puerta_6_invasor_4_2,
  input  Input_invasor_5,
  input  Puerta_3_invasor_5,
  input  Puerta_2_invasor_5,
  input  Puerta_3_invasor_5_2,
  output \Output_colisión_invasor_1 ,
  output \Output_colisión_invasor_2 ,
  output \Output_colisión_invasor_3 ,
  output \Output_colisión_invasor_4 ,
  output \Output_colisión_invasor_5 
);

  wire and_1_out, and_2_out, and_3_out, and_4_out, and_5_out, and_6_out, and_7_out, and_8_out, and_9_out,
       and_10_out, and_11_out, and_12_out, and_13_out, and_14_out, and_15_out;

  and and_1 (and_1_out, Input_invasor_1, Puerta_3_invasor_1);
  and and_2 (and_2_out, Input_invasor_1, Puerta_2_invasor_1);
  and and_3 (and_3_out, Input_invasor_1, Puerta_3_invasor_1_2);
  and and_4 (and_4_out, Input_invasor_2, Puerta_6_invasor_2);
  and and_5 (and_5_out, Input_invasor_2, Puerta_5_invasor_2);
  and and_6 (and_6_out, Input_invasor_2, Puerta_6_invasor_2_2);
  and and_7 (and_7_out, Input_invasor_3, Puerta_3_invasor_3);
  and and_8 (and_8_out, Input_invasor_3, Puerta_2_invasor_3);
  and and_9 (and_9_out, Input_invasor_3, Puerta_3_invasor_3_2);
  and and_10 (and_10_out, Input_invasor_4, Puerta_6_invasor_4);
  and and_11 (and_11_out, Input_invasor_4, Puerta_5_invasor_4);
  and and_12 (and_12_out, Input_invasor_4, Puerta_6_invasor_4_2);
  and and_13 (and_13_out, Input_invasor_5, Puerta_3_invasor_5);
  and and_14 (and_14_out, Input_invasor_5, Puerta_2_invasor_5);
  and and_15 (and_15_out, Input_invasor_5, Puerta_3_invasor_5_2);
  or or_1 (\Output_colisión_invasor_1 , and_1_out, and_2_out, and_3_out);
  or or_2 (\Output_colisión_invasor_2 , and_4_out, and_5_out, and_6_out);
  or or_3 (\Output_colisión_invasor_3 , and_7_out, and_8_out, and_9_out);
  or or_4 (\Output_colisión_invasor_4 , and_10_out, and_11_out, and_12_out);
  or or_5 (\Output_colisión_invasor_5 , and_13_out, and_14_out, and_15_out);
endmodule

module Chip_desplazamiento_bala___CDB (
  input  Input_gatillo,
  input  Input__Reset___1__Limpia_el_registro,
  input  Input_power,
  output Output_a_fila_2_splitter,
  output Output_a_fila_3_splitter,
  output Output_a_fila_4_splitter,
  output Output_a_fila_5_splitter,
  output Output_a_fila_6_splitter,
  output Output_a_fila_7_splitter,
  output \Output__Registro_activo__Sí__1 
);

  wire and_1_out, and_2_out, buffer_1_out, clock_1_out, nor_1_out, or_1_out, or_2_out;

  Clock clock_1 (.out(clock_1_out));
  and and_1 (and_1_out, clock_1_out, ~nor_1_out);  // AND_Gate
  buf buffer_1 (buffer_1_out, and_2_out);
  and and_2 (and_2_out, Input_gatillo, nor_1_out);
  or or_1 (or_1_out, buffer_1_out, and_1_out);
  nor nor_1 (nor_1_out, Output_a_fila_2_splitter, Output_a_fila_3_splitter, Output_a_fila_4_splitter, Output_a_fila_5_splitter, Output_a_fila_6_splitter, Output_a_fila_7_splitter);
  or or_2 (or_2_out, Input__Reset___1__Limpia_el_registro, ~Input_power);  // OR_Gate
  Shift_Register #(.length(6)) shift_register_1 (
    .in(and_2_out), .clk(or_1_out), .clr(or_2_out), .q0(Output_a_fila_2_splitter),
    .q1(Output_a_fila_3_splitter), .q2(Output_a_fila_4_splitter), .q3(Output_a_fila_5_splitter),
    .q4(Output_a_fila_6_splitter), .q5(Output_a_fila_7_splitter));  // open: shift, out, load, d0, d1, d2, d3, d4, d5
  or or_3 (\Output__Registro_activo__Sí__1 , Output_a_fila_7_splitter, Output_a_fila_6_splitter, Output_a_fila_5_splitter, Output_a_fila_4_splitter, Output_a_fila_3_splitter, Output_a_fila_2_splitter);

  // Notes on the sheet:
  //   Registro de la columna actual
endmodule

module Chip_Invasor___CI (
  input  Input__Apagar_nave__Apagar__1,
  input  Input_power,
  output \Output__Nave_encedida__Sí__1 
);

  wire d_ff_1_qn, not_1_out;

  D_Flip_Flop d_ff_1 (
    .clk(Input__Apagar_nave__Apagar__1), .D(Input__Apagar_nave__Apagar__1), .Qn(d_ff_1_qn), .reset(not_1_out));  // open: Q, preset, en
  not not_1 (not_1_out, Input_power);
  and and_1 (\Output__Nave_encedida__Sí__1 , d_ff_1_qn, Input_power);
endmodule

module Chip_movimiento_nave___CMN (
  input  Input_power,
  input  \Input_botón_izquierda ,
  input  \Input_botón_derecha ,
  output Output_a_splitter_1___Fila_1,
  output Output_a_splitter_2___Fila_1,
  output Output_a_splitter_3___Fila_1,
  output Output_a_splitter_4___Fila_1,
  output Output_a_splitter_5___Fila_1,
  output Output_a_splitter_6___Fila_1,
  output Output_a_splitter_7___Fila_1,
  output Output_a_splitter_8___Fila_1,
  output Output_a_splitter_9___Fila_1,
  output Output_a_splitter_10___Fila_1,
  output Output_a_splitter_11___Fila_1,
  output Output_a_splitter_12___Fila_1,
  output Output_a_splitter_13___Fila_1,
  output Output_a_splitter_14___Fila_1,
  output Output_a_splitter_15___Fila_0,
  output Output_a_splitter_0__fila_0,
  output Output_a_splitter_1___Fila_0,
  output Output_a_splitter_2___Fila_0,
  output Output_a_splitter_3___Fila_0,
  output Output_a_splitter_4___Fila_0,
  output Output_a_splitter_5___Fila_0,
  output Output_a_splitter_6___Fila_0,
  output Output_a_splitter_7___Fila_0,
  output Output_a_splitter_8___Fila_0,
  output Output_a_splitter_9___Fila_0,
  output Output_a_splitter_10___Fila_0,
  output Output_a_splitter_11___Fila_0,
  output Output_a_splitter_12___Fila_0,
  output Output_a_splitter_13___Fila_0,
  output Output_a_splitter_14___Fila_0,
  output [3:0] \Output_posición_nave 
);

  \Chip_posición_nave___CPN  \chip_posición_nave_cpn_1  (
    .\Input_botón_izquierda (\Input_botón_izquierda ), .\Input_botón_derecha (\Input_botón_derecha ),
    .\Output_posición_nave_en_la_fila (\Output_posición_nave ), .Input_power(Input_power));
  Decoder #(.select(4)) decoder_1 (
    .out1(Output_a_splitter_0__fila_0), .out2(Output_a_splitter_2___Fila_1),
    .out3(Output_a_splitter_3___Fila_1), .out4(Output_a_splitter_4___Fila_1),
    .out5(Output_a_splitter_5___Fila_1), .out6(Output_a_splitter_6___Fila_1),
    .out7(Output_a_splitter_7___Fila_1), .out8(Output_a_splitter_8___Fila_1),
    .out9(Output_a_splitter_9___Fila_1), .out10(Output_a_splitter_10___Fila_1),
    .out11(Output_a_splitter_11___Fila_1), .out12(Output_a_splitter_12___Fila_1),
    .out13(Output_a_splitter_13___Fila_1), .out14(Output_a_splitter_14___Fila_1), .sel(\Output_posición_nave ));  // open: out0, out15, en
  or _1 (Output_a_splitter_1___Fila_0, Output_a_splitter_0__fila_0, Output_a_splitter_2___Fila_1);
  or _3 (Output_a_splitter_3___Fila_0, Output_a_splitter_2___Fila_1, Output_a_splitter_3___Fila_1, Output_a_splitter_4___Fila_1);
  or _2 (Output_a_splitter_2___Fila_0, Output_a_splitter_2___Fila_1, Output_a_splitter_0__fila_0, Output_a_splitter_3___Fila_1);
  or _4 (Output_a_splitter_4___Fila_0, Output_a_splitter_4___Fila_1, Output_a_splitter_3___Fila_1, Output_a_splitter_5___Fila_1);
  or _5 (Output_a_splitter_5___Fila_0, Output_a_splitter_4___Fila_1, Output_a_splitter_5___Fila_1, Output_a_splitter_6___Fila_1);
  or _7 (Output_a_splitter_7___Fila_0, Output_a_splitter_7___Fila_1, Output_a_splitter_6___Fila_1, Output_a_splitter_8___Fila_1);
  or _6 (Output_a_splitter_6___Fila_0, Output_a_splitter_7___Fila_1, Output_a_splitter_5___Fila_1, Output_a_splitter_6___Fila_1);
  or _8 (Output_a_splitter_8___Fila_0, Output_a_splitter_7___Fila_1, Output_a_splitter_8___Fila_1, Output_a_splitter_9___Fila_1);
  or _9 (Output_a_splitter_9___Fila_0, Output_a_splitter_9___Fila_1, Output_a_splitter_10___Fila_1, Output_a_splitter_8___Fila_1);
  or _11 (Output_a_splitter_11___Fila_0, Output_a_splitter_10___Fila_1, Output_a_splitter_11___Fila_1, Output_a_splitter_12___Fila_1);
  or _10 (Output_a_splitter_10___Fila_0, Output_a_splitter_9___Fila_1, Output_a_splitter_10___Fila_1, Output_a_splitter_11___Fila_1);
  or _12 (Output_a_splitter_12___Fila_0, Output_a_splitter_11___Fila_1, Output_a_splitter_12___Fila_1, Output_a_splitter_13___Fila_1);
  or _13 (Output_a_splitter_13___Fila_0, Output_a_splitter_12___Fila_1, Output_a_splitter_13___Fila_1, Output_a_splitter_14___Fila_1);
  or _14 (Output_a_splitter_14___Fila_0, Output_a_splitter_13___Fila_1, Output_a_splitter_14___Fila_1);

  assign Output_a_splitter_1___Fila_1 = Output_a_splitter_0__fila_0;
  assign Output_a_splitter_15___Fila_0 = Output_a_splitter_14___Fila_1;

  // Notes on the sheet:
  //   sp0
  //   0
  //   _sp1_
  //   _sp2_
  //   1
  //   0
  //   1
  //   _sp3_
  //   0
  //   1
  //   0
  //   _sp4_
  //   1
  //   0
  //   _sp6_
  //   _sp5_
  //   0
  //   1
  //   1
  //   _sp7_
  //   0
  //   0
  //   1
  //   CADA OUTPUT TIENE ARRIBA LA ETIQUETA DE SU SPLITTER CORRESPONDIENTE. EL NÚMERO 0 O 1 INIDCA EL PIN DEL SPLITTER AL CUAL SE DEBE CONECTAR.
  //   _sp8_
  //   0
  //   1
  //   _sp9_
  //   _sp10_
  //   1
  //   0
  //   1
  //   _sp11_
  //   0
  //   0
  //   1
  //   _sp12_
  //   1
  //   0
  //   _sp14_
  //   _sp13_
  //   1
  //   1
  //   0
  //   sp15
  //   0
  //   0
endmodule

module \Chip_posición_nave___CPN  (
  input  \Input_botón_izquierda ,
  input  \Input_botón_derecha ,
  input  Input_power,
  output [3:0] \Output_posición_nave_en_la_fila 
);

  wire and_1_out, and_2_out, and_3_out, and_4_out, and_5_out, and_6_out, and_7_out, and_8_out, and_9_out,
       and_10_out, and_11_out, and_12_out, and_13_out, and_14_out, and_15_out, and_16_out, and_17_out,
       and_18_out, and_19_out, and_20_out, and_21_out, and_22_out, and_23_out, and_24_out, and_25_out,
       and_26_out, and_27_out, and_28_out, and_29_out, and_30_out, and_31_out, and_32_out, and_33_out,
       buffer_1_out, buffer_2_out, buffer_3_out, not_1_out, not_2_out, not_3_out, not_4_out, not_5_out,
       not_6_out, not_7_out, not_8_out, not_9_out, not_10_out, not_11_out, not_12_out, not_13_out,
       not_14_out, not_15_out, not_16_out, not_17_out, not_18_out, not_19_out, not_20_out, not_21_out,
       not_22_out, not_23_out, not_24_out, not_25_out, not_26_out, not_27_out, not_28_out, not_29_out,
       not_30_out, not_31_out, not_32_out, not_33_out, not_34_out, not_35_out, not_36_out, not_37_out,
       not_38_out, not_39_out, not_40_out, not_41_out, not_42_out, not_43_out, not_44_out, not_45_out,
       not_46_out, not_47_out, not_48_out, not_49_out, not_50_out, not_51_out, not_52_out, not_53_out,
       not_54_out, not_55_out, not_56_out, not_57_out, not_58_out, not_59_out, or_1_out, or_2_out, or_3_out,
       or_4_out, or_5_out, PWR_q;

  or or_1 (or_1_out, \Input_botón_derecha , \Input_botón_izquierda , PWR_q);
  buf buffer_1 (buffer_1_out, or_1_out);
  not not_1 (not_1_out, \Input_botón_izquierda );
  not not_2 (not_2_out, \Input_botón_izquierda );
  not not_3 (not_3_out, \Output_posición_nave_en_la_fila [2]);
  not not_4 (not_4_out, \Input_botón_izquierda );
  not not_5 (not_5_out, \Output_posición_nave_en_la_fila [1]);
  not not_6 (not_6_out, \Input_botón_izquierda );
  not not_7 (not_7_out, \Input_botón_izquierda );
  not not_8 (not_8_out, \Input_botón_derecha );
  not not_9 (not_9_out, \Output_posición_nave_en_la_fila [1]);
  not not_10 (not_10_out, \Output_posición_nave_en_la_fila [0]);
  not not_11 (not_11_out, \Output_posición_nave_en_la_fila [2]);
  not not_12 (not_12_out, \Output_posición_nave_en_la_fila [1]);
  not not_13 (not_13_out, \Output_posición_nave_en_la_fila [0]);
  not not_14 (not_14_out, \Input_botón_derecha );
  not not_15 (not_15_out, \Input_botón_izquierda );
  not not_16 (not_16_out, \Output_posición_nave_en_la_fila [1]);
  not not_17 (not_17_out, \Input_botón_izquierda );
  not not_18 (not_18_out, \Output_posición_nave_en_la_fila [0]);
  not not_19 (not_19_out, \Input_botón_izquierda );
  not not_20 (not_20_out, \Input_botón_derecha );
  not not_21 (not_21_out, \Output_posición_nave_en_la_fila [1]);
  not not_22 (not_22_out, \Output_posición_nave_en_la_fila [0]);
  not not_23 (not_23_out, \Input_botón_derecha );
  not not_24 (not_24_out, \Output_posición_nave_en_la_fila [1]);
  not not_25 (not_25_out, \Output_posición_nave_en_la_fila [0]);
  not not_26 (not_26_out, \Input_botón_derecha );
  not not_27 (not_27_out, \Input_botón_izquierda );
  not not_28 (not_28_out, \Output_posición_nave_en_la_fila [3]);
  not not_29 (not_29_out, \Output_posición_nave_en_la_fila [2]);
  not not_30 (not_30_out, \Output_posición_nave_en_la_fila [1]);
  not not_31 (not_31_out, \Output_posición_nave_en_la_fila [0]);
  not not_32 (not_32_out, \Output_posición_nave_en_la_fila [3]);
  not not_33 (not_33_out, \Output_posición_nave_en_la_fila [2]);
  not not_34 (not_34_out, \Output_posición_nave_en_la_fila [1]);
  not not_35 (not_35_out, \Input_botón_derecha );
  not not_36 (not_36_out, \Output_posición_nave_en_la_fila [3]);
  not not_37 (not_37_out, \Output_posición_nave_en_la_fila [0]);
  not not_38 (not_38_out, \Input_botón_izquierda );
  not not_39 (not_39_out, \Output_posición_nave_en_la_fila [2]);
  not not_40 (not_40_out, \Output_posición_nave_en_la_fila [0]);
  not not_41 (not_41_out, \Input_botón_izquierda );
  not not_42 (not_42_out, \Output_posición_nave_en_la_fila [1]);
  not not_43 (not_43_out, \Output_posición_nave_en_la_fila [0]);
  not not_44 (not_44_out, \Input_botón_izquierda );
  not not_45 (not_45_out, \Output_posición_nave_en_la_fila [0]);
  not not_46 (not_46_out, \Input_botón_derecha );
  not not_47 (not_47_out, \Output_posición_nave_en_la_fila [3]);
  not not_48 (not_48_out, \Input_botón_izquierda );
  not not_49 (not_49_out, \Input_botón_derecha );
  not not_50 (not_50_out, \Output_posición_nave_en_la_fila [2]);
  not not_51 (not_51_out, \Input_botón_izquierda );
  not not_52 (not_52_out, \Input_botón_derecha );
  not not_53 (not_53_out, \Output_posición_nave_en_la_fila [1]);
  not not_54 (not_54_out, \Input_botón_izquierda );
  not not_55 (not_55_out, \Input_botón_derecha );
  not not_56 (not_56_out, \Output_posición_nave_en_la_fila [3]);
  not not_57 (not_57_out, \Output_posición_nave_en_la_fila [2]);
  not not_58 (not_58_out, \Output_posición_nave_en_la_fila [1]);
  buf buffer_2 (buffer_2_out, buffer_1_out);
  buf buffer_3 (buffer_3_out, buffer_2_out);
  and and_1 (and_1_out, \Output_posición_nave_en_la_fila [2], \Output_posición_nave_en_la_fila [1], \Output_posición_nave_en_la_fila [0], not_1_out, \Input_botón_derecha );
  and and_2 (and_2_out, \Output_posición_nave_en_la_fila [3], not_2_out);
  and and_3 (and_3_out, \Output_posición_nave_en_la_fila [3], \Input_botón_derecha );
  and and_4 (and_4_out, \Output_posición_nave_en_la_fila [3], \Output_posición_nave_en_la_fila [0]);
  and and_5 (and_5_out, \Output_posición_nave_en_la_fila [3], \Output_posición_nave_en_la_fila [1]);
  and and_6 (and_6_out, \Output_posición_nave_en_la_fila [3], \Output_posición_nave_en_la_fila [2]);
  and and_7 (and_7_out, not_3_out, \Output_posición_nave_en_la_fila [1], \Output_posición_nave_en_la_fila [0], not_4_out, \Input_botón_derecha );
  and and_8 (and_8_out, \Output_posición_nave_en_la_fila [2], not_5_out, not_6_out);
  and and_9 (and_9_out, \Output_posición_nave_en_la_fila [2], not_7_out, not_8_out);
  and and_10 (and_10_out, \Output_posición_nave_en_la_fila [2], not_9_out, \Input_botón_derecha );
  and and_11 (and_11_out, \Output_posición_nave_en_la_fila [2], \Output_posición_nave_en_la_fila [0], \Input_botón_izquierda );
  and and_12 (and_12_out, \Output_posición_nave_en_la_fila [2], \Output_posición_nave_en_la_fila [1], not_10_out);
  and and_13 (and_13_out, \Output_posición_nave_en_la_fila [3], not_11_out, not_12_out, not_13_out, \Input_botón_izquierda , not_14_out);
  and and_14 (and_14_out, \Output_posición_nave_en_la_fila [3], \Output_posición_nave_en_la_fila [2], not_15_out);
  and and_15 (and_15_out, not_16_out, \Output_posición_nave_en_la_fila [0], not_17_out, \Input_botón_derecha );
  and and_16 (and_16_out, \Output_posición_nave_en_la_fila [1], not_18_out, not_19_out);
  and and_17 (and_17_out, \Output_posición_nave_en_la_fila [1], \Input_botón_izquierda , \Input_botón_derecha );
  and and_18 (and_18_out, \Output_posición_nave_en_la_fila [1], \Output_posición_nave_en_la_fila [0], not_20_out);
  and and_19 (and_19_out, \Output_posición_nave_en_la_fila [2], not_21_out, not_22_out, \Input_botón_izquierda , not_23_out);
  and and_20 (and_20_out, \Output_posición_nave_en_la_fila [3], not_24_out, not_25_out, \Input_botón_izquierda , not_26_out);
  and and_21 (and_21_out, \Output_posición_nave_en_la_fila [3], \Output_posición_nave_en_la_fila [2], \Output_posición_nave_en_la_fila [1], not_27_out);
  and and_22 (and_22_out, not_28_out, not_29_out, not_30_out, not_31_out);
  and and_23 (and_23_out, not_32_out, not_33_out, not_34_out, not_35_out);
  and and_24 (and_24_out, not_36_out, not_37_out, not_38_out, \Input_botón_derecha );
  and and_25 (and_25_out, not_39_out, not_40_out, not_41_out, \Input_botón_derecha );
  and and_26 (and_26_out, not_42_out, not_43_out, not_44_out, \Input_botón_derecha );
  and and_27 (and_27_out, not_45_out, \Input_botón_izquierda , not_46_out);
  and and_28 (and_28_out, not_47_out, \Output_posición_nave_en_la_fila [0], not_48_out, not_49_out);
  and and_29 (and_29_out, not_50_out, \Output_posición_nave_en_la_fila [0], not_51_out, not_52_out);
  and and_30 (and_30_out, not_53_out, \Output_posición_nave_en_la_fila [0], not_54_out, not_55_out);
  and and_31 (and_31_out, not_56_out, \Output_posición_nave_en_la_fila [0], \Input_botón_izquierda , \Input_botón_derecha );
  and and_32 (and_32_out, not_57_out, \Output_posición_nave_en_la_fila [0], \Input_botón_izquierda , \Input_botón_derecha );
  and and_33 (and_33_out, not_58_out, \Output_posición_nave_en_la_fila [0], \Input_botón_izquierda , \Input_botón_derecha );
  or or_2 (or_2_out, and_1_out, and_2_out, and_3_out, and_4_out, and_5_out, and_6_out);
  or or_3 (or_3_out, and_7_out, and_8_out, and_9_out, and_10_out, and_11_out, and_12_out, and_13_out, and_14_out);
  or or_4 (or_4_out, and_15_out, and_16_out, and_17_out, and_18_out, and_19_out, and_20_out, and_21_out);
  or or_5 (or_5_out, and_22_out, and_23_out, and_24_out, and_25_out, and_26_out, and_27_out, and_28_out, and_29_out, and_30_out, and_31_out, and_32_out, and_33_out);
  not not_59 (not_59_out, Input_power);
  D_Flip_Flop PWR (
    .clk(Input_power), .D(Input_power), .Q(PWR_q), .reset(\Output_posición_nave_en_la_fila [0]));  // open: Qn, preset, en
  D_Flip_Flop DA (
    .clk(buffer_3_out), .D(or_2_out), .Q(\Output_posición_nave_en_la_fila [3]), .reset(not_59_out));  // open: Qn, preset, en
  D_Flip_Flop DB (
    .clk(buffer_3_out), .D(or_3_out), .Q(\Output_posición_nave_en_la_fila [2]), .reset(not_59_out));  // open: Qn, preset, en
  D_Flip_Flop DC (
    .clk(buffer_3_out), .D(or_4_out), .Q(\Output_posición_nave_en_la_fila [1]), .reset(not_59_out));  // open: Qn, preset, en
  D_Flip_Flop DD (
    .clk(buffer_3_out), .D(or_5_out), .Q(\Output_posición_nave_en_la_fila [0]), .reset(not_59_out));  // open: Qn, preset, en

  // Notes on the sheet:
  //   Buffers para ajustar el delay al reloj
  //   IMPLEMENTA LA POSICIÓN DEL PIXEL DE LA NAVE, TOMANDO COMO REFERENCIA EL PIXEL CENTRAL DE LA MISMA.
endmodule

module Power_switch_display___PSD (
  input  Input_Power,
  input  [7:0] Input_Led_Splitter,
  input  [7:0] Input_Led_Splitter_2,
  input  [7:0] Input_Led_Splitter_3,
  input  [7:0] Input_Led_Splitter_4,
  input  [7:0] Input_Led_Splitter_5,
  input  [7:0] Input_Led_Splitter_6,
  input  [7:0] Input_Led_Splitter_7,
  input  [7:0] Input_Led_Splitter_8,
  input  [7:0] Input_Led_Splitter_9,
  input  [7:0] Input_Led_Splitter_10,
  input  [7:0] Input_Led_Splitter_11,
  input  [7:0] Input_Led_Splitter_12,
  input  [7:0] Input_Led_Splitter_13,
  input  [7:0] Input_Led_Splitter_14,
  input  [7:0] Input_Led_Splitter_15,
  input  [7:0] Input_Led_Splitter_16,
  output [7:0] Output_Led_Splitter,
  output [7:0] Output_Led_Splitter_2,
  output [7:0] Output_Led_Splitter_3,
  output [7:0] Output_Led_Splitter_4,
  output [7:0] Output_Led_Splitter_5,
  output [7:0] Output_Led_Splitter_6,
  output [7:0] Output_Led_Splitter_7,
  output [7:0] Output_Led_Splitter_8,
  output [7:0] Output_Led_Splitter_9,
  output [7:0] Output_Led_Splitter_10,
  output [7:0] Output_Led_Splitter_11,
  output [7:0] Output_Led_Splitter_12,
  output [7:0] Output_Led_Splitter_13,
  output [7:0] Output_Led_Splitter_14,
  output [7:0] Output_Led_Splitter_15,
  output [7:0] Output_Led_Splitter_16
);

  assign Output_Led_Splitter = Input_Power ? Input_Led_Splitter : 8'bz;  // Controlled_Buffer controlled_buffer_1
  assign Output_Led_Splitter_2 = Input_Power ? Input_Led_Splitter_2 : 8'bz;  // Controlled_Buffer controlled_buffer_2
  assign Output_Led_Splitter_3 = Input_Power ? Input_Led_Splitter_3 : 8'bz;  // Controlled_Buffer controlled_buffer_3
  assign Output_Led_Splitter_4 = Input_Power ? Input_Led_Splitter_4 : 8'bz;  // Controlled_Buffer controlled_buffer_4
  assign Output_Led_Splitter_5 = Input_Power ? Input_Led_Splitter_5 : 8'bz;  // Controlled_Buffer controlled_buffer_5
  assign Output_Led_Splitter_6 = Input_Power ? Input_Led_Splitter_6 : 8'bz;  // Controlled_Buffer controlled_buffer_6
  assign Output_Led_Splitter_7 = Input_Power ? Input_Led_Splitter_7 : 8'bz;  // Controlled_Buffer controlled_buffer_7
  assign Output_Led_Splitter_8 = Input_Power ? Input_Led_Splitter_8 : 8'bz;  // Controlled_Buffer controlled_buffer_8
  assign Output_Led_Splitter_9 = Input_Power ? Input_Led_Splitter_9 : 8'bz;  // Controlled_Buffer controlled_buffer_9
  assign Output_Led_Splitter_10 = Input_Power ? Input_Led_Splitter_10 : 8'bz;  // Controlled_Buffer controlled_buffer_10
  assign Output_Led_Splitter_11 = Input_Power ? Input_Led_Splitter_11 : 8'bz;  // Controlled_Buffer controlled_buffer_11
  assign Output_Led_Splitter_12 = Input_Power ? Input_Led_Splitter_12 : 8'bz;  // Controlled_Buffer controlled_buffer_12
  assign Output_Led_Splitter_13 = Input_Power ? Input_Led_Splitter_13 : 8'bz;  // Controlled_Buffer controlled_buffer_13
  assign Output_Led_Splitter_14 = Input_Power ? Input_Led_Splitter_14 : 8'bz;  // Controlled_Buffer controlled_buffer_14
  assign Output_Led_Splitter_15 = Input_Power ? Input_Led_Splitter_15 : 8'bz;  // Controlled_Buffer controlled_buffer_15
  assign Output_Led_Splitter_16 = Input_Power ? Input_Led_Splitter_16 : 8'bz;  // Controlled_Buffer controlled_buffer_16
endmodule
