// Logisim project encender_nave.circ as structural Verilog: 4 circuits, main circuit main
module main (
);

  wire button_1_out, button_2_out, decoder_1_out3;
  wire [3:0] mover_nave_1_out_3;
  wire [7:0] undriven, undriven_3;
  wire [7:2] undriven_2;

  Button button_1 (.out(button_1_out));
  Button button_2 (.out(button_2_out));
  Mover_nave mover_nave_1 (.izq(button_1_out), .der(button_2_out), .out_3(mover_nave_1_out_3));
  DotMatrix #(.matrixcols(16), .matrixrows(8)) dotmatrix_1 (
    .col0(undriven), .col1({undriven_2, {2{undriven[0]}}}), .col2(undriven_3));  // open: col3, col4, col5, col6, col7, col8, col9, col10, col11, col12, col13, col14, col15
  Decoder #(.select(4)) decoder_1 (
    .out1(undriven[0]), .out2(undriven_3[1]), .out3(decoder_1_out3), .sel(mover_nave_1_out_3));  // open: out0, out4, out5, out6, out7, out8, out9, out10, out11, out12, out13, out14, out15, en
endmodule

module Mover_nave (
  input  izq,
  input  der,
  output [3:0] out_3
);

  wire and_1_out, and_2_out, and_3_out, and_4_out, and_5_out, and_6_out, and_7_out, and_8_out, and_9_out,
       and_10_out, and_11_out, and_12_out, and_13_out, and_14_out, and_15_out, and_16_out, and_17_out,
       and_18_out, and_19_out, and_20_out, and_21_out, and_22_out, and_23_out, and_24_out, and_25_out,
       and_26_out, and_27_out, and_28_out, and_29_out, and_30_out, and_31_out, and_32_out, and_33_out,
       and_34_out, and_35_out, and_36_out, not_1_out, not_2_out, not_3_out, not_4_out, not_5_out, not_6_out,
       not_7_out, not_8_out, not_9_out, not_10_out, not_11_out, not_12_out, not_13_out, not_14_out,
       not_15_out, not_16_out, not_17_out, not_18_out, not_19_out, not_20_out, not_21_out, not_22_out,
       not_23_out, not_24_out, not_25_out, not_26_out, not_27_out, not_28_out, not_29_out, not_30_out,
       not_31_out, not_32_out, not_33_out, not_34_out, not_35_out, not_36_out, not_37_out, not_38_out,
       not_39_out, not_40_out, not_41_out, not_42_out, not_43_out, not_44_out, not_45_out, not_46_out,
       not_47_out, not_48_out, not_49_out, not_50_out, not_51_out, not_52_out, not_53_out, not_54_out,
       not_55_out, not_56_out, not_57_out, not_58_out, or_1_out, or_2_out, or_3_out, or_4_out, or_5_out;

  and and_1 (and_1_out, der, der);
  and and_2 (and_2_out, izq, izq);
  or or_1 (or_1_out, and_1_out, and_2_out);
  and and_3 (and_3_out, or_1_out, or_1_out);
  not not_1 (not_1_out, izq);
  not not_2 (not_2_out, izq);
  not not_3 (not_3_out, out_3[2]);
  not not_4 (not_4_out, izq);
  not not_5 (not_5_out, out_3[1]);
  not not_6 (not_6_out, izq);
  not not_7 (not_7_out, izq);
  not not_8 (not_8_out, der);
  not not_9 (not_9_out, out_3[1]);
  not not_10 (not_10_out, out_3[0]);
  not not_11 (not_11_out, out_3[2]);
  not not_12 (not_12_out, out_3[1]);
  not not_13 (not_13_out, out_3[0]);
  not not_14 (not_14_out, der);
  not not_15 (not_15_out, izq);
  not not_16 (not_16_out, out_3[1]);
  not not_17 (not_17_out, izq);
  not not_18 (not_18_out, out_3[0]);
  not not_19 (not_19_out, izq);
  not not_20 (not_20_out, der);
  not not_21 (not_21_out, out_3[1]);
  not not_22 (not_22_out, out_3[0]);
  not not_23 (not_23_out, der);
  not not_24 (not_24_out, out_3[1]);
  not not_25 (not_25_out, out_3[0]);
  not not_26 (not_26_out, der);
  not not_27 (not_27_out, izq);
  not not_28 (not_28_out, out_3[3]);
  not not_29 (not_29_out, out_3[2]);
  not not_30 (not_30_out, out_3[1]);
  not not_31 (not_31_out, out_3[0]);
  not not_32 (not_32_out, out_3[3]);
  not not_33 (not_33_out, out_3[2]);
  not not_34 (not_34_out, out_3[1]);
  not not_35 (not_35_out, der);
  not not_36 (not_36_out, out_3[3]);
  not not_37 (not_37_out, out_3[0]);
  not not_38 (not_38_out, izq);
  not not_39 (not_39_out, out_3[2]);
  not not_40 (not_40_out, out_3[0]);
  not not_41 (not_41_out, izq);
  not not_42 (not_42_out, out_3[1]);
  not not_43 (not_43_out, out_3[0]);
  not not_44 (not_44_out, izq);
  not not_45 (not_45_out, out_3[0]);
  not not_46 (not_46_out, der);
  not not_47 (not_47_out, out_3[3]);
  not not_48 (not_48_out, izq);
  not not_49 (not_49_out, der);
  not not_50 (not_50_out, out_3[2]);
  not not_51 (not_51_out, izq);
  not not_52 (not_52_out, der);
  not not_53 (not_53_out, out_3[1]);
  not not_54 (not_54_out, izq);
  not not_55 (not_55_out, der);
  not not_56 (not_56_out, out_3[3]);
  not not_57 (not_57_out, out_3[2]);
  not not_58 (not_58_out, out_3[1]);
  and and_4 (and_4_out, out_3[2], out_3[1], out_3[0], not_1_out, der);
  and and_5 (and_5_out, out_3[3], not_2_out);
  and and_6 (and_6_out, out_3[3], der);
  and and_7 (and_7_out, out_3[3], out_3[0]);
  and and_8 (and_8_out, out_3[3], out_3[1]);
  and and_9 (and_9_out, out_3[3], out_3[2]);
  and and_10 (and_10_out, not_3_out, out_3[1], out_3[0], not_4_out, der);
  and and_11 (and_11_out, out_3[2], not_5_out, not_6_out);
  and and_12 (and_12_out, out_3[2], not_7_out, not_8_out);
  and and_13 (and_13_out, out_3[2], not_9_out, der);
  and and_14 (and_14_out, out_3[2], out_3[0], izq);
  and and_15 (and_15_out, out_3[2], out_3[1], not_10_out);
  and and_16 (and_16_out, out_3[3], not_11_out, not_12_out, not_13_out, izq, not_14_out);
  and and_17 (and_17_out, out_3[3], out_3[2], not_15_out);
  and and_18 (and_18_out, not_16_out, out_3[0], not_17_out, der);
  and and_19 (and_19_out, out_3[1], not_18_out, not_19_out);
  and and_20 (and_20_out, out_3[1], izq, der);
  and and_21 (and_21_out, out_3[1], out_3[0], not_20_out);
  and and_22 (and_22_out, out_3[2], not_21_out, not_22_out, izq, not_23_out);
  and and_23 (and_23_out, out_3[3], not_24_out, not_25_out, izq, not_26_out);
  and and_24 (and_24_out, out_3[3], out_3[2], out_3[1], not_27_out);
  and and_25 (and_25_out, not_28_out, not_29_out, not_30_out, not_31_out);
  and and_26 (and_26_out, not_32_out, not_33_out, not_34_out, not_35_out);
  and and_27 (and_27_out, not_36_out, not_37_out, not_38_out, der);
  and and_28 (and_28_out, not_39_out, not_40_out, not_41_out, der);
  and and_29 (and_29_out, not_42_out, not_43_out, not_44_out, der);
  and and_30 (and_30_out, not_45_out, izq, not_46_out);
  and and_31 (and_31_out, not_47_out, out_3[0], not_48_out, not_49_out);
  and and_32 (and_32_out, not_50_out, out_3[0], not_51_out, not_52_out);
  and and_33 (and_33_out, not_53_out, out_3[0], not_54_out, not_55_out);
  and and_34 (and_34_out, not_56_out, out_3[0], izq, der);
  and and_35 (and_35_out, not_57_out, out_3[0], izq, der);
  and and_36 (and_36_out, not_58_out, out_3[0], izq, der);
  or or_2 (or_2_out, and_4_out, and_5_out, and_6_out, and_7_out, and_8_out, and_9_out);
  or or_3 (or_3_out, and_18_out, and_19_out, and_20_out, and_21_out, and_22_out, and_23_out, and_24_out);
  or or_4 (or_4_out, and_10_out, and_11_out, and_12_out, and_13_out, and_14_out, and_15_out, and_16_out, and_17_out);
  or or_5 (or_5_out, and_25_out, and_26_out, and_27_out, and_28_out, and_29_out, and_30_out, and_31_out, and_32_out, and_33_out, and_34_out, and_35_out, and_36_out);
  D_Flip_Flop DA (.clk(and_3_out), .D(or_2_out), .Q(out_3[3]));  // open: Qn, preset, en, reset
  D_Flip_Flop DB (.clk(and_3_out), .D(or_4_out), .Q(out_3[2]));  // open: Qn, preset, en, reset
  D_Flip_Flop DC (.clk(and_3_out), .D(or_3_out), .Q(out_3[1]));  // open: Qn, preset, en, reset
  D_Flip_Flop DD (.clk(and_3_out), .D(or_5_out), .Q(out_3[0]));  // open: Qn, preset, en, reset

  // Notes on the sheet:
  //   posición centro de nave
endmodule

module Mover_nave_original (
  input  QA,
  input  QB,
  input  QC,
  input  QD,
  input  Izq,
  input  Der,
  output DA,
  output DB,
  output DC,
  output DD
);

  wire and_1_out, and_2_out, and_3_out, and_4_out, and_5_out, and_6_out, and_7_out, and_8_out, and_9_out,
       and_10_out, and_11_out, and_12_out, and_13_out, and_14_out, and_15_out, and_16_out, and_17_out,
       and_18_out, and_19_out, and_20_out, and_21_out, and_22_out, and_23_out, and_24_out, and_25_out,
       and_26_out, and_27_out, and_28_out, and_29_out, and_30_out, and_31_out, and_32_out, and_33_out,
       not_1_out, not_2_out, not_3_out, not_4_out, not_5_out, not_6_out, not_7_out, not_8_out, not_9_out,
       not_10_out, not_11_out, not_12_out, not_13_out, not_14_out, not_15_out, not_16_out, not_17_out,
       not_18_out, not_19_out, not_20_out, not_21_out, not_22_out, not_23_out, not_24_out, not_25_out,
       not_26_out, not_27_out, not_28_out, not_29_out, not_30_out, not_31_out, not_32_out, not_33_out,
       not_34_out, not_35_out, not_36_out, not_37_out, not_38_out, not_39_out, not_40_out, not_41_out,
       not_42_out, not_43_out, not_44_out, not_45_out, not_46_out, not_47_out, not_48_out, not_49_out,
       not_50_out, not_51_out, not_52_out, not_53_out, not_54_out, not_55_out, not_56_out, not_57_out,
       not_58_out;

  not not_1 (not_1_out, Izq);
  not not_2 (not_2_out, Izq);
  not not_3 (not_3_out, QB);
  not not_4 (not_4_out, Izq);
  not not_5 (not_5_out, QC);
  not not_6 (not_6_out, Izq);
  not not_7 (not_7_out, Izq);
  not not_8 (not_8_out, Der);
  not not_9 (not_9_out, QC);
  not not_10 (not_10_out, QD);
  not not_11 (not_11_out, QB);
  not not_12 (not_12_out, QC);
  not not_13 (not_13_out, QD);
  not not_14 (not_14_out, Der);
  not not_15 (not_15_out, Izq);
  not not_16 (not_16_out, QC);
  not not_17 (not_17_out, Izq);
  not not_18 (not_18_out, QD);
  not not_19 (not_19_out, Izq);
  not not_20 (not_20_out, Der);
  not not_21 (not_21_out, QC);
  not not_22 (not_22_out, QD);
  not not_23 (not_23_out, Der);
  not not_24 (not_24_out, QC);
  not not_25 (not_25_out, QD);
  not not_26 (not_26_out, Der);
  not not_27 (not_27_out, Izq);
  not not_28 (not_28_out, QA);
  not not_29 (not_29_out, QB);
  not not_30 (not_30_out, QC);
  not not_31 (not_31_out, QD);
  not not_32 (not_32_out, QA);
  not not_33 (not_33_out, QB);
  not not_34 (not_34_out, QC);
  not not_35 (not_35_out, Der);
  not not_36 (not_36_out, QA);
  not not_37 (not_37_out, QD);
  not not_38 (not_38_out, Izq);
  not not_39 (not_39_out, QB);
  not not_40 (not_40_out, QD);
  not not_41 (not_41_out, Izq);
  not not_42 (not_42_out, QC);
  not not_43 (not_43_out, QD);
  not not_44 (not_44_out, Izq);
  not not_45 (not_45_out, QD);
  not not_46 (not_46_out, Der);
  not not_47 (not_47_out, QA);
  not not_48 (not_48_out, Izq);
  not not_49 (not_49_out, Der);
  not not_50 (not_50_out, QB);
  not not_51 (not_51_out, Izq);
  not not_52 (not_52_out, Der);
  not not_53 (not_53_out, QC);
  not not_54 (not_54_out, Izq);
  not not_55 (not_55_out, Der);
  not not_56 (not_56_out, QA);
  not not_57 (not_57_out, QB);
  not not_58 (not_58_out, QC);
  and and_1 (and_1_out, QB, QC, QD, not_1_out, Der);
  and and_2 (and_2_out, QA, not_2_out);
  and and_3 (and_3_out, QA, Der);
  and and_4 (and_4_out, QA, QD);
  and and_5 (and_5_out, QA, QC);
  and and_6 (and_6_out, QA, QB);
  and and_7 (and_7_out, not_3_out, QC, QD, not_4_out, Der);
  and and_8 (and_8_out, QB, not_5_out, not_6_out);
  and and_9 (and_9_out, QB, not_7_out, not_8_out);
  and and_10 (and_10_out, QB, not_9_out, Der);
  and and_11 (and_11_out, QB, QD, Izq);
  and and_12 (and_12_out, QB, QC, not_10_out);
  and and_13 (and_13_out, QA, not_11_out, not_12_out, not_13_out, Izq, not_14_out);
  and and_14 (and_14_out, QA, QB, not_15_out);
  and and_15 (and_15_out, not_16_out, QD, not_17_out, Der);
  and and_16 (and_16_out, QC, not_18_out, not_19_out);
  and and_17 (and_17_out, QC, Izq, Der);
  and and_18 (and_18_out, QC, QD, not_20_out);
  and and_19 (and_19_out, QB, not_21_out, not_22_out, Izq, not_23_out);
  and and_20 (and_20_out, QA, not_24_out, not_25_out, Izq, not_26_out);
  and and_21 (and_21_out, QA, QB, QC, not_27_out);
  and and_22 (and_22_out, not_28_out, not_29_out, not_30_out, not_31_out);
  and and_23 (and_23_out, not_32_out, not_33_out, not_34_out, not_35_out);
  and and_24 (and_24_out, not_36_out, not_37_out, not_38_out, Der);
  and and_25 (and_25_out, not_39_out, not_40_out, not_41_out, Der);
  and and_26 (and_26_out, not_42_out, not_43_out, not_44_out, Der);
  and and_27 (and_27_out, not_45_out, Izq, not_46_out);
  and and_28 (and_28_out, not_47_out, QD, not_48_out, not_49_out);
  and and_29 (and_29_out, not_50_out, QD, not_51_out, not_52_out);
  and and_30 (and_30_out, not_53_out, QD, not_54_out, not_55_out);
  and and_31 (and_31_out, not_56_out, QD, Izq, Der);
  and and_32 (and_32_out, not_57_out, QD, Izq, Der);
  and and_33 (and_33_out, not_58_out, QD, Izq, Der);
  or or_1 (DA, and_1_out, and_2_out, and_3_out, and_4_out, and_5_out, and_6_out);
  or or_2 (DB, and_7_out, and_8_out, and_9_out, and_10_out, and_11_out, and_12_out, and_13_out, and_14_out);
  or or_3 (DC, and_15_out, and_16_out, and_17_out, and_18_out, and_19_out, and_20_out, and_21_out);
  or or_4 (DD, and_22_out, and_23_out, and_24_out, and_25_out, and_26_out, and_27_out, and_28_out, and_29_out, and_30_out, and_31_out, and_32_out, and_33_out);
endmodule

module Encender_nave (
);

  wire button_1_out, button_2_out, decoder_1_out0;
  wire [3:0] mover_nave_1_out_3;
  wire [7:0] _0_out, _1_out, _2_out, _3_out, _4_out, _5_out, _6_out, _7_out, _8_out, _9_out, _10_out,
       _11_out, _12_out, _13_out, _14_out, _15_out;

  Button button_1 (.out(button_1_out));
  Button button_2 (.out(button_2_out));
  Mover_nave mover_nave_1 (.izq(button_1_out), .der(button_2_out), .out_3(mover_nave_1_out_3));
  Decoder #(.select(4)) decoder_1 (
    .out0(decoder_1_out0), .out1(_1_out[1]), .out2(_2_out[1]), .out3(_3_out[1]), .out4(_4_out[1]),
    .out5(_5_out[1]), .out6(_6_out[1]), .out7(_7_out[1]), .out8(_8_out[1]), .out9(_9_out[1]),
    .out10(_10_out[1]), .out11(_11_out[1]), .out12(_12_out[1]), .out13(_13_out[1]), .out14(_14_out[1]),
    .out15(_15_out[1]), .sel(mover_nave_1_out_3));  // open: en
  or _0 (_0_out[0], decoder_1_out0, _1_out[1]);
  or _1 (_1_out[0], _1_out[1], _2_out[1]);
  or _2 (_2_out[0], _2_out[1], _1_out[1], _3_out[1]);
  or _3 (_3_out[0], _2_out[1], _3_out[1], _4_out[1]);
  DotMatrix #(.matrixcols(16), .matrixrows(8)) dotmatrix_1 (
    .col0(_0_out), .col1(_1_out), .col2(_2_out), .col3(_3_out), .col4(_4_out), .col5(_5_out), .col6(_6_out),
    .col7(_7_out), .col8(_8_out), .col9(_9_out), .col10(_10_out), .col11(_11_out), .col12(_12_out),
    .col13(_13_out), .col14(_14_out), .col15(_15_out));
  or _4 (_4_out[0], _4_out[1], _3_out[1], _5_out[1]);
  or _5 (_5_out[0], _4_out[1], _5_out[1], _6_out[1]);
  or _6 (_6_out[0], _7_out[1], _5_out[1], _6_out[1]);
  or _7 (_7_out[0], _7_out[1], _6_out[1], _8_out[1]);
  or _8 (_8_out[0], _7_out[1], _8_out[1], _9_out[1]);
  or _9 (_9_out[0], _9_out[1], _10_out[1], _8_out[1]);
  or _10 (_10_out[0], _9_out[1], _10_out[1], _11_out[1]);
  or _11 (_11_out[0], _10_out[1], _11_out[1], _12_out[1]);
  or _12 (_12_out[0], _11_out[1], _12_out[1], _13_out[1]);
  or _13 (_13_out[0], _12_out[1], _13_out[1], _14_out[1]);
  or _14 (_14_out[0], _13_out[1], _14_out[1], _15_out[1]);
  or _15 (_15_out[0], _14_out[1], _15_out[1]);
endmodule
