// Logisim project mover _nave_test_reloj.circ as structural Verilog
module Mover_nave (
);

  wire and_1_out, and_2_out, and_3_out, and_4_out, and_5_out, and_6_out, and_7_out, and_8_out, and_9_out,
       and_10_out, and_11_out, and_12_out, and_13_out, and_14_out, and_15_out, and_16_out, and_17_out,
       and_18_out, and_19_out, and_20_out, and_21_out, and_22_out, and_23_out, and_24_out, and_25_out,
       and_26_out, and_27_out, and_28_out, and_29_out, and_30_out, and_31_out, and_32_out, and_33_out,
       and_34_out, and_35_out, and_36_out, and_37_out, and_38_out, DA_q, DB_prime_q, DC_q, DD_q, Der_out,
       Izq_out, not_1_out, not_2_out, not_3_out, not_4_out, not_5_out, not_6_out, not_7_out, not_8_out,
       not_9_out, not_10_out, not_11_out, not_12_out, not_13_out, not_14_out, not_15_out, not_16_out,
       not_17_out, not_18_out, not_19_out, not_20_out, not_21_out, not_22_out, not_23_out, not_24_out,
       not_25_out, not_26_out, not_27_out, not_28_out, not_29_out, not_30_out, not_31_out, not_32_out,
       not_33_out, not_34_out, not_35_out, not_36_out, not_37_out, not_38_out, not_39_out, not_40_out,
       not_41_out, not_42_out, not_43_out, not_44_out, not_45_out, not_46_out, not_47_out, not_48_out,
       not_49_out, not_50_out, not_51_out, or_1_out, or_2_out, or_3_out, or_4_out, or_5_out, or_6_out;

  and and_1 (and_1_out, DD_q, DD_q);
  and and_2 (and_2_out, DB_prime_q, DB_prime_q);
  and and_3 (and_3_out, DC_q, DC_q);
  and and_4 (and_4_out, DA_q, DA_q);
  or or_1 (or_1_out, and_1_out, and_2_out, and_3_out, and_4_out);
  Button Izq (.out(Izq_out));
  Button Der (.out(Der_out));
  buf and_5 (and_5_out, or_1_out);  // AND_Gate
  and and_6 (and_6_out, or_1_out, or_1_out);
  or or_2 (or_2_out, and_5_out, and_5_out, and_6_out, and_6_out);
  not not_1 (not_1_out, Izq_out);
  not not_2 (not_2_out, Izq_out);
  not not_3 (not_3_out, DB_prime_q);
  not not_4 (not_4_out, Izq_out);
  not not_5 (not_5_out, DC_q);
  not not_6 (not_6_out, Izq_out);
  not not_7 (not_7_out, Izq_out);
  not not_8 (not_8_out, Der_out);
  not not_9 (not_9_out, DC_q);
  not not_10 (not_10_out, DD_q);
  not not_11 (not_11_out, DB_prime_q);
  not not_12 (not_12_out, DC_q);
  not not_13 (not_13_out, DD_q);
  not not_14 (not_14_out, Der_out);
  not not_15 (not_15_out, Izq_out);
  not not_16 (not_16_out, DC_q);
  not not_17 (not_17_out, Izq_out);
  not not_18 (not_18_out, DD_q);
  not not_19 (not_19_out, Izq_out);
  not not_20 (not_20_out, Der_out);
  not not_21 (not_21_out, DC_q);
  not not_22 (not_22_out, DD_q);
  not not_23 (not_23_out, Der_out);
  not not_24 (not_24_out, DC_q);
  not not_25 (not_25_out, DD_q);
  not not_26 (not_26_out, Der_out);
  not not_27 (not_27_out, Izq_out);
  not not_28 (not_28_out, DA_q);
  not not_29 (not_29_out, DB_prime_q);
  not not_30 (not_30_out, DC_q);
  not not_31 (not_31_out, DD_q);
  not not_32 (not_32_out, DA_q);
  not not_33 (not_33_out, DB_prime_q);
  not not_34 (not_34_out, DC_q);
  not not_35 (not_35_out, Der_out);
  not not_36 (not_36_out, DD_q);
  not not_37 (not_37_out, Izq_out);
  not not_38 (not_38_out, DD_q);
  not not_39 (not_39_out, Der_out);
  not not_40 (not_40_out, DA_q);
  not not_41 (not_41_out, Izq_out);
  not not_42 (not_42_out, Der_out);
  not not_43 (not_43_out, DB_prime_q);
  not not_44 (not_44_out, Izq_out);
  not not_45 (not_45_out, Der_out);
  not not_46 (not_46_out, DC_q);
  not not_47 (not_47_out, Izq_out);
  not not_48 (not_48_out, Der_out);
  not not_49 (not_49_out, DA_q);
  not not_50 (not_50_out, DB_prime_q);
  not not_51 (not_51_out, DC_q);
  and and_7 (and_7_out, DB_prime_q, DC_q, DD_q, not_1_out, Der_out);
  and and_8 (and_8_out, DA_q, not_2_out);
  and and_9 (and_9_out, DA_q, Der_out);
  and and_10 (and_10_out, DA_q, DD_q);
  and and_11 (and_11_out, DA_q, DC_q);
  and and_12 (and_12_out, DA_q, DB_prime_q);
  and and_13 (and_13_out, not_3_out, DC_q, DD_q, not_4_out, Der_out);
  and and_14 (and_14_out, DB_prime_q, not_5_out, not_6_out);
  and and_15 (and_15_out, DB_prime_q, not_7_out, not_8_out);
  and and_16 (and_16_out, DB_prime_q, not_9_out, Der_out);
  and and_17 (and_17_out, DB_prime_q, DD_q, Izq_out);
  and and_18 (and_18_out, DB_prime_q, DC_q, not_10_out);
  and and_19 (and_19_out, DA_q, not_11_out, not_12_out, not_13_out, Izq_out, not_14_out);
  and and_20 (and_20_out, DA_q, DB_prime_q, not_15_out);
  and and_21 (and_21_out, not_16_out, DD_q, not_17_out, Der_out);
  and and_22 (and_22_out, DC_q, not_18_out, not_19_out);
  and and_23 (and_23_out, DC_q, Izq_out, Der_out);
  and and_24 (and_24_out, DC_q, DD_q, not_20_out);
  and and_25 (and_25_out, DB_prime_q, not_21_out, not_22_out, Izq_out, not_23_out);
  and and_26 (and_26_out, DA_q, not_24_out, not_25_out, Izq_out, not_26_out);
  and and_27 (and_27_out, DA_q, DB_prime_q, DC_q, not_27_out);
  and and_28 (and_28_out, not_28_out, not_29_out, not_30_out, not_31_out);
  and and_29 (and_29_out, not_32_out, not_33_out, not_34_out, not_35_out);
  and and_30 (and_30_out, not_36_out, not_37_out, Der_out);
  and and_31 (and_31_out, not_38_out, Izq_out, not_39_out);
  and and_32 (and_32_out, not_40_out, DD_q, not_41_out, not_42_out);
  and and_33 (and_33_out, not_43_out, DD_q, not_44_out, not_45_out);
  and and_34 (and_34_out, not_46_out, DD_q, not_47_out, not_48_out);
  and and_35 (and_35_out, not_49_out, DD_q, Izq_out, Der_out);
  and and_36 (and_36_out, not_50_out, DD_q, Izq_out, Der_out);
  and and_37 (and_37_out, not_51_out, DD_q, Izq_out, Der_out);
  or or_3 (or_3_out, and_7_out, and_8_out, and_9_out, and_10_out, and_11_out, and_12_out);
  or or_4 (or_4_out, and_13_out, and_14_out, and_15_out, and_16_out, and_17_out, and_18_out, and_19_out, and_20_out);
  or or_5 (or_5_out, and_21_out, and_22_out, and_23_out, and_24_out, and_25_out, and_26_out, and_27_out);
  or or_6 (or_6_out, and_28_out, and_29_out, and_30_out, and_31_out, and_32_out, and_33_out, and_34_out, and_35_out, and_36_out, and_37_out);
  and and_38 (and_38_out, or_2_out, or_2_out);
  D_Flip_Flop DC (.clk(and_38_out), .D(or_5_out), .Q(DC_q));  // open: Qn, preset, en, reset
  D_Flip_Flop DA (.clk(and_38_out), .D(or_3_out), .Q(DA_q));  // open: Qn, preset, en, reset
  D_Flip_Flop DB_prime (.clk(and_38_out), .D(or_4_out), .Q(DB_prime_q));  // open: Qn, preset, en, reset
  D_Flip_Flop DD (.clk(and_38_out), .D(or_6_out), .Q(DD_q));  // open: Qn, preset, en, reset
endmodule

module Mover_nave_2 (
  input  QA,
  input  QB,
  input  QC,
  input  QD,
  output DA,
  output DB,
  output DC,
  output DD
);

  wire and_1_out, and_2_out, and_3_out, and_4_out, and_5_out, and_6_out, and_7_out, and_8_out, and_9_out,
       and_10_out, and_11_out, and_12_out, and_13_out, and_14_out, and_15_out, and_16_out, and_17_out,
       and_18_out, and_19_out, and_20_out, and_21_out, and_22_out, and_23_out, and_24_out, and_25_out,
       and_26_out, and_27_out, and_28_out, and_29_out, and_30_out, and_31_out, and_32_out, and_33_out,
       button_1_out, button_2_out, not_1_out, not_2_out, not_3_out, not_4_out, not_5_out, not_6_out,
       not_7_out, not_8_out, not_9_out, not_10_out, not_11_out, not_12_out, not_13_out, not_14_out,
       not_15_out, not_16_out, not_17_out, not_18_out, not_19_out, not_20_out, not_21_out, not_22_out,
       not_23_out, not_24_out, not_25_out, not_26_out, not_27_out, not_28_out, not_29_out, not_30_out,
       not_31_out, not_32_out, not_33_out, not_34_out, not_35_out, not_36_out, not_37_out, not_38_out,
       not_39_out, not_40_out, not_41_out, not_42_out, not_43_out, not_44_out, not_45_out, not_46_out,
       not_47_out, not_48_out, not_49_out, not_50_out, not_51_out, not_52_out, not_53_out, not_54_out,
       not_55_out, not_56_out, not_57_out, not_58_out;

  Button button_1 (.out(button_1_out));
  Button button_2 (.out(button_2_out));
  not not_1 (not_1_out, button_1_out);
  not not_2 (not_2_out, button_1_out);
  not not_3 (not_3_out, QB);
  not not_4 (not_4_out, button_1_out);
  not not_5 (not_5_out, QC);
  not not_6 (not_6_out, button_1_out);
  not not_7 (not_7_out, button_1_out);
  not not_8 (not_8_out, button_2_out);
  not not_9 (not_9_out, QC);
  not not_10 (not_10_out, QD);
  not not_11 (not_11_out, QB);
  not not_12 (not_12_out, QC);
  not not_13 (not_13_out, QD);
  not not_14 (not_14_out, button_2_out);
  not not_15 (not_15_out, button_1_out);
  not not_16 (not_16_out, QC);
  not not_17 (not_17_out, button_1_out);
  not not_18 (not_18_out, QD);
  not not_19 (not_19_out, button_1_out);
  not not_20 (not_20_out, button_2_out);
  not not_21 (not_21_out, QC);
  not not_22 (not_22_out, QD);
  not not_23 (not_23_out, button_2_out);
  not not_24 (not_24_out, QC);
  not not_25 (not_25_out, QD);
  not not_26 (not_26_out, button_2_out);
  not not_27 (not_27_out, button_1_out);
  not not_28 (not_28_out, QA);
  not not_29 (not_29_out, QB);
  not not_30 (not_30_out, QC);
  not not_31 (not_31_out, QD);
  not not_32 (not_32_out, QA);
  not not_33 (not_33_out, QB);
  not not_34 (not_34_out, QC);
  not not_35 (not_35_out, button_2_out);
  not not_36 (not_36_out, QA);
  not not_37 (not_37_out, QD);
  not not_38 (not_38_out, button_1_out);
  not not_39 (not_39_out, QB);
  not not_40 (not_40_out, QD);
  not not_41 (not_41_out, button_1_out);
  not not_42 (not_42_out, QC);
  not not_43 (not_43_out, QD);
  not not_44 (not_44_out, button_1_out);
  not not_45 (not_45_out, QD);
  not not_46 (not_46_out, button_2_out);
  not not_47 (not_47_out, QA);
  not not_48 (not_48_out, button_1_out);
  not not_49 (not_49_out, button_2_out);
  not not_50 (not_50_out, QB);
  not not_51 (not_51_out, button_1_out);
  not not_52 (not_52_out, button_2_out);
  not not_53 (not_53_out, QC);
  not not_54 (not_54_out, button_1_out);
  not not_55 (not_55_out, button_2_out);
  not not_56 (not_56_out, QA);
  not not_57 (not_57_out, QB);
  not not_58 (not_58_out, QC);
  and and_1 (and_1_out, QB, QC, QD, not_1_out, button_2_out);
  and and_2 (and_2_out, QA, not_2_out);
  and and_3 (and_3_out, QA, button_2_out);
  and and_4 (and_4_out, QA, QD);
  and and_5 (and_5_out, QA, QC);
  and and_6 (and_6_out, QA, QB);
  and and_7 (and_7_out, not_3_out, QC, QD, not_4_out, button_2_out);
  and and_8 (and_8_out, QB, not_5_out, not_6_out);
  and and_9 (and_9_out, QB, not_7_out, not_8_out);
  and and_10 (and_10_out, QB, not_9_out, button_2_out);
  and and_11 (and_11_out, QB, QD, button_1_out);
  and and_12 (and_12_out, QB, QC, not_10_out);
  and and_13 (and_13_out, QA, not_11_out, not_12_out, not_13_out, button_1_out, not_14_out);
  and and_14 (and_14_out, QA, QB, not_15_out);
  and and_15 (and_15_out, not_16_out, QD, not_17_out, button_2_out);
  and and_16 (and_16_out, QC, not_18_out, not_19_out);
  and and_17 (and_17_out, QC, button_1_out, button_2_out);
  and and_18 (and_18_out, QC, QD, not_20_out);
  and and_19 (and_19_out, QB, not_21_out, not_22_out, button_1_out, not_23_out);
  and and_20 (and_20_out, QA, not_24_out, not_25_out, button_1_out, not_26_out);
  and and_21 (and_21_out, QA, QB, QC, not_27_out);
  and and_22 (and_22_out, not_28_out, not_29_out, not_30_out, not_31_out);
  and and_23 (and_23_out, not_32_out, not_33_out, not_34_out, not_35_out);
  and and_24 (and_24_out, not_36_out, not_37_out, not_38_out, button_2_out);
  and and_25 (and_25_out, not_39_out, not_40_out, not_41_out, button_2_out);
  and and_26 (and_26_out, not_42_out, not_43_out, not_44_out, button_2_out);
  and and_27 (and_27_out, not_45_out, button_1_out, not_46_out);
  and and_28 (and_28_out, not_47_out, QD, not_48_out, not_49_out);
  and and_29 (and_29_out, not_50_out, QD, not_51_out, not_52_out);
  and and_30 (and_30_out, not_53_out, QD, not_54_out, not_55_out);
  and and_31 (and_31_out, not_56_out, QD, button_1_out, button_2_out);
  and and_32 (and_32_out, not_57_out, QD, button_1_out, button_2_out);
  and and_33 (and_33_out, not_58_out, QD, button_1_out, button_2_out);
  or or_1 (DA, and_1_out, and_2_out, and_3_out, and_4_out, and_5_out, and_6_out);
  or or_2 (DB, and_7_out, and_8_out, and_9_out, and_10_out, and_11_out, and_12_out, and_13_out, and_14_out);
  or or_3 (DC, and_15_out, and_16_out, and_17_out, and_18_out, and_19_out, and_20_out, and_21_out);
  or or_4 (DD, and_22_out, and_23_out, and_24_out, and_25_out, and_26_out, and_27_out, and_28_out, and_29_out, and_30_out, and_31_out, and_32_out, and_33_out);
endmodule

module Mover_nave_3 (
  input  QA,
  input  QB,
  input  QC,
  input  QD,
  input  Izq,
  input  Der,
  output DA,
  output DB,
  output DC,
  output DD
);

  wire and_1_out, and_2_out, and_3_out, and_4_out, and_5_out, and_6_out, and_7_out, and_8_out, and_9_out,
       and_10_out, and_11_out, and_12_out, and_13_out, and_14_out, and_15_out, and_16_out, and_17_out,
       and_18_out, and_19_out, and_20_out, and_21_out, and_22_out, and_23_out, and_24_out, and_25_out,
       and_26_out, and_27_out, and_28_out, and_29_out, and_30_out, and_31_out, and_32_out, and_33_out,
       not_1_out, not_2_out, not_3_out, not_4_out, not_5_out, not_6_out, not_7_out, not_8_out, not_9_out,
       not_10_out, not_11_out, not_12_out, not_13_out, not_14_out, not_15_out, not_16_out, not_17_out,
       not_18_out, not_19_out, not_20_out, not_21_out, not_22_out, not_23_out, not_24_out, not_25_out,
       not_26_out, not_27_out, not_28_out, not_29_out, not_30_out, not_31_out, not_32_out, not_33_out,
       not_34_out, not_35_out, not_36_out, not_37_out, not_38_out, not_39_out, not_40_out, not_41_out,
       not_42_out, not_43_out, not_44_out, not_45_out, not_46_out, not_47_out, not_48_out, not_49_out,
       not_50_out, not_51_out, not_52_out, not_53_out, not_54_out, not_55_out, not_56_out, not_57_out,
       not_58_out;

  not not_1 (not_1_out, Izq);
  not not_2 (not_2_out, Izq);
  not not_3 (not_3_out, QB);
  not not_4 (not_4_out, Izq);
  not not_5 (not_5_out, QC);
  not not_6 (not_6_out, Izq);
  not not_7 (not_7_out, Izq);
  not not_8 (not_8_out, Der);
  not not_9 (not_9_out, QC);
  not not_10 (not_10_out, QD);
  not not_11 (not_11_out, QB);
  not not_12 (not_12_out, QC);
  not not_13 (not_13_out, QD);
  not not_14 (not_14_out, Der);
  not not_15 (not_15_out, Izq);
  not not_16 (not_16_out, QC);
  not not_17 (not_17_out, Izq);
  not not_18 (not_18_out, QD);
  not not_19 (not_19_out, Izq);
  not not_20 (not_20_out, Der);
  not not_21 (not_21_out, QC);
  not not_22 (not_22_out, QD);
  not not_23 (not_23_out, Der);
  not not_24 (not_24_out, QC);
  not not_25 (not_25_out, QD);
  not not_26 (not_26_out, Der);
  not not_27 (not_27_out, Izq);
  not not_28 (not_28_out, QA);
  not not_29 (not_29_out, QB);
  not not_30 (not_30_out, QC);
  not not_31 (not_31_out, QD);
  not not_32 (not_32_out, QA);
  not not_33 (not_33_out, QB);
  not not_34 (not_34_out, QC);
  not not_35 (not_35_out, Der);
  not not_36 (not_36_out, QA);
  not not_37 (not_37_out, QD);
  not not_38 (not_38_out, Izq);
  not not_39 (not_39_out, QB);
  not not_40 (not_40_out, QD);
  not not_41 (not_41_out, Izq);
  not not_42 (not_42_out, QC);
  not not_43 (not_43_out, QD);
  not not_44 (not_44_out, Izq);
  not not_45 (not_45_out, QD);
  not not_46 (not_46_out, Der);
  not not_47 (not_47_out, QA);
  not not_48 (not_48_out, Izq);
  not not_49 (not_49_out, Der);
  not not_50 (not_50_out, QB);
  not not_51 (not_51_out, Izq);
  not not_52 (not_52_out, Der);
  not not_53 (not_53_out, QC);
  not not_54 (not_54_out, Izq);
  not not_55 (not_55_out, Der);
  not not_56 (not_56_out, QA);
  not not_57 (not_57_out, QB);
  not not_58 (not_58_out, QC);
  and and_1 (and_1_out, QB, QC, QD, not_1_out, Der);
  and and_2 (and_2_out, QA, not_2_out);
  and and_3 (and_3_out, QA, Der);
  and and_4 (and_4_out, QA, QD);
  and and_5 (and_5_out, QA, QC);
  and and_6 (and_6_out, QA, QB);
  and and_7 (and_7_out, not_3_out, QC, QD, not_4_out, Der);
  and and_8 (and_8_out, QB, not_5_out, not_6_out);
  and and_9 (and_9_out, QB, not_7_out, not_8_out);
  and and_10 (and_10_out, QB, not_9_out, Der);
  and and_11 (and_11_out, QB, QD, Izq);
  and and_12 (and_12_out, QB, QC, not_10_out);
  and and_13 (and_13_out, QA, not_11_out, not_12_out, not_13_out, Izq, not_14_out);
  and and_14 (and_14_out, QA, QB, not_15_out);
  and and_15 (and_15_out, not_16_out, QD, not_17_out, Der);
  and and_16 (and_16_out, QC, not_18_out, not_19_out);
  and and_17 (and_17_out, QC, Izq, Der);
  and and_18 (and_18_out, QC, QD, not_20_out);
  and and_19 (and_19_out, QB, not_21_out, not_22_out, Izq, not_23_out);
  and and_20 (and_20_out, QA, not_24_out, not_25_out, Izq, not_26_out);
  and and_21 (and_21_out, QA, QB, QC, not_27_out);
  and and_22 (and_22_out, not_28_out, not_29_out, not_30_out, not_31_out);
  and and_23 (and_23_out, not_32_out, not_33_out, not_34_out, not_35_out);
  and and_24 (and_24_out, not_36_out, not_37_out, not_38_out, Der);
  and and_25 (and_25_out, not_39_out, not_40_out, not_41_out, Der);
  and and_26 (and_26_out, not_42_out, not_43_out, not_44_out, Der);
  and and_27 (and_27_out, not_45_out, Izq, not_46_out);
  and and_28 (and_28_out, not_47_out, QD, not_48_out, not_49_out);
  and and_29 (and_29_out, not_50_out, QD, not_51_out, not_52_out);
  and and_30 (and_30_out, not_53_out, QD, not_54_out, not_55_out);
  and and_31 (and_31_out, not_56_out, QD, Izq, Der);
  and and_32 (and_32_out, not_57_out, QD, Izq, Der);
  and and_33 (and_33_out, not_58_out, QD, Izq, Der);
  or or_1 (DA, and_1_out, and_2_out, and_3_out, and_4_out, and_5_out, and_6_out);
  or or_2 (DB, and_7_out, and_8_out, and_9_out, and_10_out, and_11_out, and_12_out, and_13_out, and_14_out);
  or or_3 (DC, and_15_out, and_16_out, and_17_out, and_18_out, and_19_out, and_20_out, and_21_out);
  or or_4 (DD, and_22_out, and_23_out, and_24_out, and_25_out, and_26_out, and_27_out, and_28_out, and_29_out, and_30_out, and_31_out, and_32_out, and_33_out);
endmodule
