// Logisim project mover_nave.circ as structural Verilog
// Izq
module Mover_nave (
);

  wire and_1_out, and_2_out, and_3_out, and_4_out, and_5_out, and_6_out, and_7_out, and_8_out, and_9_out,
       and_10_out, and_11_out, and_12_out, and_13_out, and_14_out, and_15_out, and_16_out, and_17_out,
       and_18_out, and_19_out, and_20_out, and_21_out, and_22_out, and_23_out, and_24_out, and_25_out,
       and_26_out, and_27_out, and_28_out, and_29_out, and_30_out, and_31_out, and_32_out, and_33_out,
       and_34_out, and_35_out, and_36_out, decoder_1_out0, decoder_1_out1, decoder_1_out2, decoder_1_out3,
       decoder_1_out4, decoder_1_out5, decoder_1_out6, decoder_1_out7, decoder_1_out8, decoder_1_out9,
       decoder_1_out10, decoder_1_out11, decoder_1_out12, decoder_1_out13, decoder_1_out14, decoder_1_out15,
       Der_out, Izq_out, not_1_out, not_2_out, not_3_out, not_4_out, not_5_out, not_6_out, not_7_out,
       not_8_out, not_9_out, not_10_out, not_11_out, not_12_out, not_13_out, not_14_out, not_15_out,
       not_16_out, not_17_out, not_18_out, not_19_out, not_20_out, not_21_out, not_22_out, not_23_out,
       not_24_out, not_25_out, not_26_out, not_27_out, not_28_out, not_29_out, not_30_out, not_31_out,
       not_32_out, not_33_out, not_34_out, not_35_out, not_36_out, not_37_out, not_38_out, not_39_out,
       not_40_out, not_41_out, not_42_out, not_43_out, not_44_out, not_45_out, not_46_out, not_47_out,
       not_48_out, not_49_out, not_50_out, not_51_out, not_52_out, not_53_out, not_54_out, not_55_out,
       not_56_out, not_57_out, not_58_out, or_1_out, or_2_out, or_3_out, or_4_out, or_5_out;
  wire [3:0] DD_q;

  and and_1 (and_1_out, Der_out, Der_out);
  and and_2 (and_2_out, Izq_out, Izq_out);
  Button Izq (.out(Izq_out));
  Button Der (.out(Der_out));
  or or_1 (or_1_out, and_1_out, and_2_out);
  and and_3 (and_3_out, or_1_out, or_1_out);
  not not_1 (not_1_out, Izq_out);
  not not_2 (not_2_out, Izq_out);
  not not_3 (not_3_out, DD_q[2]);
  not not_4 (not_4_out, Izq_out);
  not not_5 (not_5_out, DD_q[1]);
  not not_6 (not_6_out, Izq_out);
  not not_7 (not_7_out, Izq_out);
  not not_8 (not_8_out, Der_out);
  not not_9 (not_9_out, DD_q[1]);
  not not_10 (not_10_out, DD_q[0]);
  not not_11 (not_11_out, DD_q[2]);
  not not_12 (not_12_out, DD_q[1]);
  not not_13 (not_13_out, DD_q[0]);
  not not_14 (not_14_out, Der_out);
  not not_15 (not_15_out, Izq_out);
  not not_16 (not_16_out, DD_q[1]);
  not not_17 (not_17_out, Izq_out);
  not not_18 (not_18_out, DD_q[0]);
  not not_19 (not_19_out, Izq_out);
  not not_20 (not_20_out, Der_out);
  not not_21 (not_21_out, DD_q[1]);
  not not_22 (not_22_out, DD_q[0]);
  not not_23 (not_23_out, Der_out);
  not not_24 (not_24_out, DD_q[1]);
  not not_25 (not_25_out, DD_q[0]);
  not not_26 (not_26_out, Der_out);
  not not_27 (not_27_out, Izq_out);
  not not_28 (not_28_out, DD_q[3]);
  not not_29 (not_29_out, DD_q[2]);
  not not_30 (not_30_out, DD_q[1]);
  not not_31 (not_31_out, DD_q[0]);
  not not_32 (not_32_out, DD_q[3]);
  not not_33 (not_33_out, DD_q[2]);
  not not_34 (not_34_out, DD_q[1]);
  not not_35 (not_35_out, Der_out);
  not not_36 (not_36_out, DD_q[3]);
  not not_37 (not_37_out, DD_q[0]);
  not not_38 (not_38_out, Izq_out);
  not not_39 (not_39_out, DD_q[2]);
  not not_40 (not_40_out, DD_q[0]);
  not not_41 (not_41_out, Izq_out);
  not not_42 (not_42_out, DD_q[1]);
  not not_43 (not_43_out, DD_q[0]);
  not not_44 (not_44_out, Izq_out);
  not not_45 (not_45_out, DD_q[0]);
  not not_46 (not_46_out, Der_out);
  not not_47 (not_47_out, DD_q[3]);
  not not_48 (not_48_out, Izq_out);
  not not_49 (not_49_out, Der_out);
  not not_50 (not_50_out, DD_q[2]);
  not not_51 (not_51_out, Izq_out);
  not not_52 (not_52_out, Der_out);
  not not_53 (not_53_out, DD_q[1]);
  not not_54 (not_54_out, Izq_out);
  not not_55 (not_55_out, Der_out);
  not not_56 (not_56_out, DD_q[3]);
  not not_57 (not_57_out, DD_q[2]);
  not not_58 (not_58_out, DD_q[1]);
  and and_4 (and_4_out, DD_q[2], DD_q[1], DD_q[0], not_1_out, Der_out);
  and and_5 (and_5_out, DD_q[3], not_2_out);
  and and_6 (and_6_out, DD_q[3], Der_out);
  and and_7 (and_7_out, DD_q[3], DD_q[0]);
  and and_8 (and_8_out, DD_q[3], DD_q[1]);
  and and_9 (and_9_out, DD_q[3], DD_q[2]);
  and and_10 (and_10_out, not_3_out, DD_q[1], DD_q[0], not_4_out, Der_out);
  and and_11 (and_11_out, DD_q[2], not_5_out, not_6_out);
  and and_12 (and_12_out, DD_q[2], not_7_out, not_8_out);
  and and_13 (and_13_out, DD_q[2], not_9_out, Der_out);
  and and_14 (and_14_out, DD_q[2], DD_q[0], Izq_out);
  and and_15 (and_15_out, DD_q[2], DD_q[1], not_10_out);
  and and_16 (and_16_out, DD_q[3], not_11_out, not_12_out, not_13_out, Izq_out, not_14_out);
  and and_17 (and_17_out, DD_q[3], DD_q[2], not_15_out);
  and and_18 (and_18_out, not_16_out, DD_q[0], not_17_out, Der_out);
  and and_19 (and_19_out, DD_q[1], not_18_out, not_19_out);
  and and_20 (and_20_out, DD_q[1], Izq_out, Der_out);
  and and_21 (and_21_out, DD_q[1], DD_q[0], not_20_out);
  and and_22 (and_22_out, DD_q[2], not_21_out, not_22_out, Izq_out, not_23_out);
  and and_23 (and_23_out, DD_q[3], not_24_out, not_25_out, Izq_out, not_26_out);
  and and_24 (and_24_out, DD_q[3], DD_q[2], DD_q[1], not_27_out);
  and and_25 (and_25_out, not_28_out, not_29_out, not_30_out, not_31_out);
  and and_26 (and_26_out, not_32_out, not_33_out, not_34_out, not_35_out);
  and and_27 (and_27_out, not_36_out, not_37_out, not_38_out, Der_out);
  and and_28 (and_28_out, not_39_out, not_40_out, not_41_out, Der_out);
  and and_29 (and_29_out, not_42_out, not_43_out, not_44_out, Der_out);
  and and_30 (and_30_out, not_45_out, Izq_out, not_46_out);
  and and_31 (and_31_out, not_47_out, DD_q[0], not_48_out, not_49_out);
  and and_32 (and_32_out, not_50_out, DD_q[0], not_51_out, not_52_out);
  and and_33 (and_33_out, not_53_out, DD_q[0], not_54_out, not_55_out);
  and and_34 (and_34_out, not_56_out, DD_q[0], Izq_out, Der_out);
  and and_35 (and_35_out, not_57_out, DD_q[0], Izq_out, Der_out);
  and and_36 (and_36_out, not_58_out, DD_q[0], Izq_out, Der_out);
  or or_2 (or_2_out, and_4_out, and_5_out, and_6_out, and_7_out, and_8_out, and_9_out);
  or or_3 (or_3_out, and_18_out, and_19_out, and_20_out, and_21_out, and_22_out, and_23_out, and_24_out);
  or or_4 (or_4_out, and_10_out, and_11_out, and_12_out, and_13_out, and_14_out, and_15_out, and_16_out, and_17_out);
  or or_5 (or_5_out, and_25_out, and_26_out, and_27_out, and_28_out, and_29_out, and_30_out, and_31_out, and_32_out, and_33_out, and_34_out, and_35_out, and_36_out);
  D_Flip_Flop DA (.clk(and_3_out), .D(or_2_out), .Q(DD_q[3]));  // open: Qn, preset, en, reset
  D_Flip_Flop DB (.clk(and_3_out), .D(or_4_out), .Q(DD_q[2]));  // open: Qn, preset, en, reset
  D_Flip_Flop DC (.clk(and_3_out), .D(or_3_out), .Q(DD_q[1]));  // open: Qn, preset, en, reset
  D_Flip_Flop DD (.clk(and_3_out), .D(or_5_out), .Q(DD_q[0]));  // open: Qn, preset, en, reset
  Decoder #(.select(4)) decoder_1 (
    .out0(decoder_1_out0), .out1(decoder_1_out1), .out2(decoder_1_out2), .out3(decoder_1_out3),
    .out4(decoder_1_out4), .out5(decoder_1_out5), .out6(decoder_1_out6), .out7(decoder_1_out7),
    .out8(decoder_1_out8), .out9(decoder_1_out9), .out10(decoder_1_out10), .out11(decoder_1_out11),
    .out12(decoder_1_out12), .out13(decoder_1_out13), .out14(decoder_1_out14), .out15(decoder_1_out15),
    .sel(DD_q));  // open: en
  DotMatrix #(.matrixcols(16), .matrixrows(8)) dotmatrix_1 ();  // open: col0, col1, col2, col3, col4, col5, col6, col7, col8, col9, col10, col11, col12, col13, col14, col15
endmodule

module Mover_nave_original (
  input  QA,
  input  QB,
  input  QC,
  input  QD,
  input  Izq,
  input  Der,
  output DA,
  output DB,
  output DC,
  output DD
);

  wire and_1_out, and_2_out, and_3_out, and_4_out, and_5_out, and_6_out, and_7_out, and_8_out, and_9_out,
       and_10_out, and_11_out, and_12_out, and_13_out, and_14_out, and_15_out, and_16_out, and_17_out,
       and_18_out, and_19_out, and_20_out, and_21_out, and_22_out, and_23_out, and_24_out, and_25_out,
       and_26_out, and_27_out, and_28_out, and_29_out, and_30_out, and_31_out, and_32_out, and_33_out,
       not_1_out, not_2_out, not_3_out, not_4_out, not_5_out, not_6_out, not_7_out, not_8_out, not_9_out,
       not_10_out, not_11_out, not_12_out, not_13_out, not_14_out, not_15_out, not_16_out, not_17_out,
       not_18_out, not_19_out, not_20_out, not_21_out, not_22_out, not_23_out, not_24_out, not_25_out,
       not_26_out, not_27_out, not_28_out, not_29_out, not_30_out, not_31_out, not_32_out, not_33_out,
       not_34_out, not_35_out, not_36_out, not_37_out, not_38_out, not_39_out, not_40_out, not_41_out,
       not_42_out, not_43_out, not_44_out, not_45_out, not_46_out, not_47_out, not_48_out, not_49_out,
       not_50_out, not_51_out, not_52_out, not_53_out, not_54_out, not_55_out, not_56_out, not_57_out,
       not_58_out;

  not not_1 (not_1_out, Izq);
  not not_2 (not_2_out, Izq);
  not not_3 (not_3_out, QB);
  not not_4 (not_4_out, Izq);
  not not_5 (not_5_out, QC);
  not not_6 (not_6_out, Izq);
  not not_7 (not_7_out, Izq);
  not not_8 (not_8_out, Der);
  not not_9 (not_9_out, QC);
  not not_10 (not_10_out, QD);
  not not_11 (not_11_out, QB);
  not not_12 (not_12_out, QC);
  not not_13 (not_13_out, QD);
  not not_14 (not_14_out, Der);
  not not_15 (not_15_out, Izq);
  not not_16 (not_16_out, QC);
  not not_17 (not_17_out, Izq);
  not not_18 (not_18_out, QD);
  not not_19 (not_19_out, Izq);
  not not_20 (not_20_out, Der);
  not not_21 (not_21_out, QC);
  not not_22 (not_22_out, QD);
  not not_23 (not_23_out, Der);
  not not_24 (not_24_out, QC);
  not not_25 (not_25_out, QD);
  not not_26 (not_26_out, Der);
  not not_27 (not_27_out, Izq);
  not not_28 (not_28_out, QA);
  not not_29 (not_29_out, QB);
  not not_30 (not_30_out, QC);
  not not_31 (not_31_out, QD);
  not not_32 (not_32_out, QA);
  not not_33 (not_33_out, QB);
  not not_34 (not_34_out, QC);
  not not_35 (not_35_out, Der);
  not not_36 (not_36_out, QA);
  not not_37 (not_37_out, QD);
  not not_38 (not_38_out, Izq);
  not not_39 (not_39_out, QB);
  not not_40 (not_40_out, QD);
  not not_41 (not_41_out, Izq);
  not not_42 (not_42_out, QC);
  not not_43 (not_43_out, QD);
  not not_44 (not_44_out, Izq);
  not not_45 (not_45_out, QD);
  not not_46 (not_46_out, Der);
  not not_47 (not_47_out, QA);
  not not_48 (not_48_out, Izq);
  not not_49 (not_49_out, Der);
  not not_50 (not_50_out, QB);
  not not_51 (not_51_out, Izq);
  not not_52 (not_52_out, Der);
  not not_53 (not_53_out, QC);
  not not_54 (not_54_out, Izq);
  not not_55 (not_55_out, Der);
  not not_56 (not_56_out, QA);
  not not_57 (not_57_out, QB);
  not not_58 (not_58_out, QC);
  and and_1 (and_1_out, QB, QC, QD, not_1_out, Der);
  and and_2 (and_2_out, QA, not_2_out);
  and and_3 (and_3_out, QA, Der);
  and and_4 (and_4_out, QA, QD);
  and and_5 (and_5_out, QA, QC);
  and and_6 (and_6_out, QA, QB);
  and and_7 (and_7_out, not_3_out, QC, QD, not_4_out, Der);
  and and_8 (and_8_out, QB, not_5_out, not_6_out);
  and and_9 (and_9_out, QB, not_7_out, not_8_out);
  and and_10 (and_10_out, QB, not_9_out, Der);
  and and_11 (and_11_out, QB, QD, Izq);
  and and_12 (and_12_out, QB, QC, not_10_out);
  and and_13 (and_13_out, QA, not_11_out, not_12_out, not_13_out, Izq, not_14_out);
  and and_14 (and_14_out, QA, QB, not_15_out);
  and and_15 (and_15_out, not_16_out, QD, not_17_out, Der);
  and and_16 (and_16_out, QC, not_18_out, not_19_out);
  and and_17 (and_17_out, QC, Izq, Der);
  and and_18 (and_18_out, QC, QD, not_20_out);
  and and_19 (and_19_out, QB, not_21_out, not_22_out, Izq, not_23_out);
  and and_20 (and_20_out, QA, not_24_out, not_25_out, Izq, not_26_out);
  and and_21 (and_21_out, QA, QB, QC, not_27_out);
  and and_22 (and_22_out, not_28_out, not_29_out, not_30_out, not_31_out);
  and and_23 (and_23_out, not_32_out, not_33_out, not_34_out, not_35_out);
  and and_24 (and_24_out, not_36_out, not_37_out, not_38_out, Der);
  and and_25 (and_25_out, not_39_out, not_40_out, not_41_out, Der);
  and and_26 (and_26_out, not_42_out, not_43_out, not_44_out, Der);
  and and_27 (and_27_out, not_45_out, Izq, not_46_out);
  and and_28 (and_28_out, not_47_out, QD, not_48_out, not_49_out);
  and and_29 (and_29_out, not_50_out, QD, not_51_out, not_52_out);
  and and_30 (and_30_out, not_53_out, QD, not_54_out, not_55_out);
  and and_31 (and_31_out, not_56_out, QD, Izq, Der);
  and and_32 (and_32_out, not_57_out, QD, Izq, Der);
  and and_33 (and_33_out, not_58_out, QD, Izq, Der);
  or or_1 (DA, and_1_out, and_2_out, and_3_out, and_4_out, and_5_out, and_6_out);
  or or_2 (DB, and_7_out, and_8_out, and_9_out, and_10_out, and_11_out, and_12_out, and_13_out, and_14_out);
  or or_3 (DC, and_15_out, and_16_out, and_17_out, and_18_out, and_19_out, and_20_out, and_21_out);
  or or_4 (DD, and_22_out, and_23_out, and_24_out, and_25_out, and_26_out, and_27_out, and_28_out, and_29_out, and_30_out, and_31_out, and_32_out, and_33_out);
endmodule
